// Logisim project ETFStudent.circ as structural Verilog: 29 circuits, main circuit REG32_LD
module REG32_LD (
  input  [31:0] I15__0,
  input  LD,
  input  mr,
  input  CLK,
  output [31:0] A15__0
);

  // ETF_REG16_LD reg16_ld_1: pin names not known; wires that end beside it: CLK, mr, I15__0[31:16], A15__0[31:16], LD
  // ETF_REG16_LD reg16_ld_2: pin names not known; wires that end beside it: CLK, mr, I15__0[15:0], A15__0[15:0], LD

  // Notes on the sheet:
  //   __
endmodule

module KMADR (
  input  immed,
  input  memdir,
  input  regdir,
  input  regindpom,
  output [3:0] Adr3__0
);

  assign Adr3__0 = immed ? 4'b0010 : 4'bz;  // Controlled_Buffer controlled_buffer_1
  assign Adr3__0 = memdir ? 4'b0100 : 4'bz;  // Controlled_Buffer controlled_buffer_2
  assign Adr3__0 = regdir ? 4'b0101 : 4'bz;  // Controlled_Buffer controlled_buffer_3
  assign Adr3__0 = regindpom ? 4'b0111 : 4'bz;  // Controlled_Buffer controlled_buffer_4
endmodule

module KMOPR (
  input  LD,
  input  ST,
  input  ADD,
  input  SUB,
  input  BLSS,
  input  JLEQ,
  input  JMP,
  input  JSR,
  input  RTS,
  input  RTI,
  input  HALT,
  output [5:0] Adr5__0
);

  assign Adr5__0 = LD ? 6'b000010 : 6'bz;  // Controlled_Buffer controlled_buffer_1
  assign Adr5__0 = ST ? 6'b000100 : 6'bz;  // Controlled_Buffer controlled_buffer_2
  assign Adr5__0 = ADD ? 6'b001010 : 6'bz;  // Controlled_Buffer controlled_buffer_3
  assign Adr5__0 = SUB ? 6'b001100 : 6'bz;  // Controlled_Buffer controlled_buffer_4
  assign Adr5__0 = BLSS ? 6'b001110 : 6'bz;  // Controlled_Buffer controlled_buffer_5
  assign Adr5__0 = JLEQ ? 6'b010000 : 6'bz;  // Controlled_Buffer controlled_buffer_6
  assign Adr5__0 = JMP ? 6'b010001 : 6'bz;  // Controlled_Buffer controlled_buffer_7
  assign Adr5__0 = JSR ? 6'b010010 : 6'bz;  // Controlled_Buffer controlled_buffer_8
  assign Adr5__0 = RTS ? 6'b010111 : 6'bz;  // Controlled_Buffer controlled_buffer_9
  assign Adr5__0 = RTI ? 6'b011110 : 6'bz;  // Controlled_Buffer controlled_buffer_10
  assign Adr5__0 = HALT ? 6'b100010 : 6'bz;  // Controlled_Buffer controlled_buffer_11
endmodule

module REG6_INC_LD (
  input  [5:0] I5__0,
  input  LD,
  input  INC,
  input  mr,
  input  CLK,
  output [5:0] A5__0
);

  wire reg2m_inc_ld_1_p7, reg2m_inc_ld_2_p8;

  // REG2m_INC_LD reg2m_inc_ld_1: pin names not known; wires that end beside it: CLK, mr, I5__0[5:4], A5__0[5:4], LD, INC, reg2m_inc_ld_1_p7
  // REG2m_INC_LD reg2m_inc_ld_2: pin names not known; wires that end beside it: CLK, reg2m_inc_ld_1_p7, mr, I5__0[3:2], A5__0[3:2], LD, INC, reg2m_inc_ld_2_p8
  // REG2m_INC_LD reg2m_inc_ld_3: pin names not known; wires that end beside it: CLK, reg2m_inc_ld_2_p8, mr, I5__0[1:0], A5__0[1:0], LD, INC, INC

  // Notes on the sheet:
  //   __
endmodule

module MEM64Kx16 (
  input  WR_RD,
  input  [15:0] A15__0,
  input  [15:0] DIN,
  input  CS,
  input  CLK,
  output [15:0] DOUT
);

  wire not_1_out;

  RAM #(.addrWidth(16), .dataWidth(16), .bus("separate")) ram_1 (
    .addr(A15__0), .din(DIN), .data(DOUT), .str(WR_RD), .sel(CS), .clk(CLK), .ld(not_1_out), .clr(1'b0));
  not not_1 (not_1_out, WR_RD);

  // Notes on the sheet:
  //   __
endmodule

module ROM16x16 (
  input  [3:0] A6__0,
  input  CS,
  output [15:0] DOUT
);

  ROM #(.addrWidth(4), .dataWidth(16)) rom_1 (.addr(A6__0), .data(DOUT), .sel(CS));
endmodule

module ROM16x20 (
  input  [3:0] A6__0,
  input  CS,
  output [19:0] DOUT
);

  ROM #(.addrWidth(4), .dataWidth(20)) rom_1 (.addr(A6__0), .data(DOUT), .sel(CS));
endmodule

module ROM16x24 (
  input  [3:0] A6__0,
  input  CS,
  output [23:0] DOUT
);

  ROM #(.addrWidth(4), .dataWidth(24)) rom_1 (.addr(A6__0), .data(DOUT), .sel(CS));
endmodule

module ROM64x48 (
  input  [5:0] A6__0,
  input  CS,
  output [31:0] DOUT1,
  output [15:0] DOUT2
);

  ROM #(.addrWidth(6), .dataWidth(32)) rom_1 (.addr(A6__0), .data(DOUT1), .sel(CS));
  ROM #(.addrWidth(6), .dataWidth(16)) rom_2 (.addr(A6__0), .data(DOUT2), .sel(CS));
endmodule

module ROM64x52 (
  input  [5:0] A6__0,
  input  CS,
  output [31:0] DOUT1,
  output [19:0] DOUT2
);

  ROM #(.addrWidth(6), .dataWidth(32)) rom_1 (.addr(A6__0), .data(DOUT1), .sel(CS));
  ROM #(.addrWidth(6), .dataWidth(20)) rom_2 (.addr(A6__0), .data(DOUT2), .sel(CS));
endmodule

module SIGPASS16 (
  input  in_1,
  input  in_2,
  input  in_3,
  input  in_4,
  input  in_5,
  input  in_6,
  input  in_7,
  input  in_8,
  output out_9,
  output out_10,
  output out_11,
  output out_12,
  output out_13,
  output out_14,
  output out_15,
  output out_16
);

  Pull_Resistor pull_resistor_1 (.node(in_2));
  Pull_Resistor pull_resistor_2 (.node(in_4));
  Pull_Resistor pull_resistor_3 (.node(in_6));
  Pull_Resistor pull_resistor_4 (.node(in_8));
  Pull_Resistor pull_resistor_5 (.node(in_1));
  Pull_Resistor pull_resistor_6 (.node(in_3));
  Pull_Resistor pull_resistor_7 (.node(in_5));
  Pull_Resistor pull_resistor_8 (.node(in_7));
  assign out_9 = in_1 ? 1'b1 : 1'bz;  // Controlled_Buffer controlled_buffer_1
  assign out_10 = in_2 ? 1'b1 : 1'bz;  // Controlled_Buffer controlled_buffer_2
  assign out_11 = in_3 ? 1'b1 : 1'bz;  // Controlled_Buffer controlled_buffer_3
  assign out_12 = in_4 ? 1'b1 : 1'bz;  // Controlled_Buffer controlled_buffer_4
  assign out_13 = in_5 ? 1'b1 : 1'bz;  // Controlled_Buffer controlled_buffer_5
  assign out_14 = in_6 ? 1'b1 : 1'bz;  // Controlled_Buffer controlled_buffer_6
  assign out_15 = in_7 ? 1'b1 : 1'bz;  // Controlled_Buffer controlled_buffer_7
  assign out_16 = in_8 ? 1'b1 : 1'bz;  // Controlled_Buffer controlled_buffer_8
endmodule

module REASIGN8x4 (
  input  in_1,
  input  [3:0] in_2,
  input  in_3,
  input  [3:0] in_4,
  input  in_5,
  input  [3:0] in_6,
  input  in_7,
  input  [3:0] in_8,
  input  in_9,
  input  [3:0] in_10,
  input  in_11,
  input  [3:0] in_12,
  input  in_13,
  input  [3:0] in_14,
  input  in_15,
  input  [3:0] in_16,
  output [3:0] out_17
);

  Pull_Resistor pull_resistor_1 (.node(in_1));
  assign out_17 = in_1 ? in_2 : 4'bz;  // Controlled_Buffer controlled_buffer_1
  Pull_Resistor pull_resistor_2 (.node(in_3));
  assign out_17 = in_3 ? in_4 : 4'bz;  // Controlled_Buffer controlled_buffer_2
  Pull_Resistor pull_resistor_3 (.node(in_5));
  Pull_Resistor pull_resistor_4 (.node(in_7));
  assign out_17 = in_5 ? in_6 : 4'bz;  // Controlled_Buffer controlled_buffer_3
  Pull_Resistor pull_resistor_5 (.node(in_9));
  assign out_17 = in_7 ? in_8 : 4'bz;  // Controlled_Buffer controlled_buffer_4
  Pull_Resistor pull_resistor_6 (.node(in_11));
  assign out_17 = in_9 ? in_10 : 4'bz;  // Controlled_Buffer controlled_buffer_5
  assign out_17 = in_11 ? in_12 : 4'bz;  // Controlled_Buffer controlled_buffer_6
  Pull_Resistor pull_resistor_7 (.node(in_13));
  assign out_17 = in_13 ? in_14 : 4'bz;  // Controlled_Buffer controlled_buffer_7
  Pull_Resistor pull_resistor_8 (.node(in_15));
  assign out_17 = in_15 ? in_16 : 4'bz;  // Controlled_Buffer controlled_buffer_8
endmodule

module REASIGN32x6 (
  input  in_1,
  input  [5:0] in_2,
  input  in_3,
  input  [5:0] in_4,
  input  in_5,
  input  [5:0] in_6,
  input  in_7,
  input  [5:0] in_8,
  input  in_9,
  input  [5:0] in_10,
  input  in_11,
  input  [5:0] in_12,
  input  in_13,
  input  [5:0] in_14,
  input  in_15,
  input  [5:0] in_16,
  input  in_17,
  input  [5:0] in_18,
  input  in_19,
  input  [5:0] in_20,
  input  in_21,
  input  [5:0] in_22,
  input  in_23,
  input  [5:0] in_24,
  input  in_25,
  input  [5:0] in_26,
  input  in_27,
  input  [5:0] in_28,
  input  in_29,
  input  [5:0] in_30,
  input  in_31,
  input  [5:0] in_32,
  input  in_33,
  input  [5:0] in_34,
  input  in_35,
  input  [5:0] in_36,
  input  in_37,
  input  [5:0] in_38,
  input  in_39,
  input  [5:0] in_40,
  input  in_41,
  input  [5:0] in_42,
  input  in_43,
  input  [5:0] in_44,
  input  in_45,
  input  [5:0] in_46,
  input  in_47,
  input  [5:0] in_48,
  input  in_49,
  input  [5:0] in_50,
  input  in_51,
  input  [5:0] in_52,
  input  in_53,
  input  [5:0] in_54,
  input  in_55,
  input  [5:0] in_56,
  input  in_57,
  input  [5:0] in_58,
  input  in_59,
  input  [5:0] in_60,
  input  in_61,
  input  [5:0] in_62,
  input  in_63,
  input  [5:0] in_64,
  output [5:0] out_65
);

  Pull_Resistor pull_resistor_1 (.node(in_1));
  assign out_65 = in_1 ? in_2 : 6'bz;  // Controlled_Buffer controlled_buffer_1
  Pull_Resistor pull_resistor_2 (.node(in_3));
  assign out_65 = in_3 ? in_4 : 6'bz;  // Controlled_Buffer controlled_buffer_2
  Pull_Resistor pull_resistor_3 (.node(in_5));
  Pull_Resistor pull_resistor_4 (.node(in_7));
  assign out_65 = in_5 ? in_6 : 6'bz;  // Controlled_Buffer controlled_buffer_3
  Pull_Resistor pull_resistor_5 (.node(in_9));
  assign out_65 = in_7 ? in_8 : 6'bz;  // Controlled_Buffer controlled_buffer_4
  Pull_Resistor pull_resistor_6 (.node(in_11));
  assign out_65 = in_9 ? in_10 : 6'bz;  // Controlled_Buffer controlled_buffer_5
  assign out_65 = in_11 ? in_12 : 6'bz;  // Controlled_Buffer controlled_buffer_6
  Pull_Resistor pull_resistor_7 (.node(in_13));
  assign out_65 = in_13 ? in_14 : 6'bz;  // Controlled_Buffer controlled_buffer_7
  Pull_Resistor pull_resistor_8 (.node(in_15));
  assign out_65 = in_15 ? in_16 : 6'bz;  // Controlled_Buffer controlled_buffer_8
  Pull_Resistor pull_resistor_9 (.node(in_17));
  assign out_65 = in_17 ? in_18 : 6'bz;  // Controlled_Buffer controlled_buffer_9
  Pull_Resistor pull_resistor_10 (.node(in_19));
  assign out_65 = in_19 ? in_20 : 6'bz;  // Controlled_Buffer controlled_buffer_10
  Pull_Resistor pull_resistor_11 (.node(in_21));
  Pull_Resistor pull_resistor_12 (.node(in_23));
  assign out_65 = in_21 ? in_22 : 6'bz;  // Controlled_Buffer controlled_buffer_11
  Pull_Resistor pull_resistor_13 (.node(in_25));
  assign out_65 = in_23 ? in_24 : 6'bz;  // Controlled_Buffer controlled_buffer_12
  Pull_Resistor pull_resistor_14 (.node(in_27));
  assign out_65 = in_25 ? in_26 : 6'bz;  // Controlled_Buffer controlled_buffer_13
  assign out_65 = in_27 ? in_28 : 6'bz;  // Controlled_Buffer controlled_buffer_14
  Pull_Resistor pull_resistor_15 (.node(in_29));
  assign out_65 = in_29 ? in_30 : 6'bz;  // Controlled_Buffer controlled_buffer_15
  Pull_Resistor pull_resistor_16 (.node(in_31));
  assign out_65 = in_31 ? in_32 : 6'bz;  // Controlled_Buffer controlled_buffer_16
  Pull_Resistor pull_resistor_17 (.node(in_33));
  assign out_65 = in_33 ? in_34 : 6'bz;  // Controlled_Buffer controlled_buffer_17
  Pull_Resistor pull_resistor_18 (.node(in_35));
  assign out_65 = in_35 ? in_36 : 6'bz;  // Controlled_Buffer controlled_buffer_18
  Pull_Resistor pull_resistor_19 (.node(in_37));
  Pull_Resistor pull_resistor_20 (.node(in_39));
  assign out_65 = in_37 ? in_38 : 6'bz;  // Controlled_Buffer controlled_buffer_19
  Pull_Resistor pull_resistor_21 (.node(in_41));
  assign out_65 = in_39 ? in_40 : 6'bz;  // Controlled_Buffer controlled_buffer_20
  Pull_Resistor pull_resistor_22 (.node(in_43));
  assign out_65 = in_41 ? in_42 : 6'bz;  // Controlled_Buffer controlled_buffer_21
  assign out_65 = in_43 ? in_44 : 6'bz;  // Controlled_Buffer controlled_buffer_22
  Pull_Resistor pull_resistor_23 (.node(in_45));
  assign out_65 = in_45 ? in_46 : 6'bz;  // Controlled_Buffer controlled_buffer_23
  Pull_Resistor pull_resistor_24 (.node(in_47));
  assign out_65 = in_47 ? in_48 : 6'bz;  // Controlled_Buffer controlled_buffer_24
  Pull_Resistor pull_resistor_25 (.node(in_49));
  assign out_65 = in_49 ? in_50 : 6'bz;  // Controlled_Buffer controlled_buffer_25
  Pull_Resistor pull_resistor_26 (.node(in_51));
  assign out_65 = in_51 ? in_52 : 6'bz;  // Controlled_Buffer controlled_buffer_26
  Pull_Resistor pull_resistor_27 (.node(in_53));
  Pull_Resistor pull_resistor_28 (.node(in_55));
  assign out_65 = in_53 ? in_54 : 6'bz;  // Controlled_Buffer controlled_buffer_27
  Pull_Resistor pull_resistor_29 (.node(in_57));
  assign out_65 = in_55 ? in_56 : 6'bz;  // Controlled_Buffer controlled_buffer_28
  Pull_Resistor pull_resistor_30 (.node(in_59));
  assign out_65 = in_57 ? in_58 : 6'bz;  // Controlled_Buffer controlled_buffer_29
  assign out_65 = in_59 ? in_60 : 6'bz;  // Controlled_Buffer controlled_buffer_30
  Pull_Resistor pull_resistor_31 (.node(in_61));
  assign out_65 = in_61 ? in_62 : 6'bz;  // Controlled_Buffer controlled_buffer_31
  Pull_Resistor pull_resistor_32 (.node(in_63));
  assign out_65 = in_63 ? in_64 : 6'bz;  // Controlled_Buffer controlled_buffer_32
endmodule

module REG16_LD (
  input  in_1,
  input  [15:0] in_2,
  input  CLK,
  input  LD,
  output [15:0] out_5
);

  Register #(.width(16)) register_1 (.D(in_2), .en(LD), .Q(out_5), .clk(CLK), .clr(in_1));
endmodule

module REG16_LD_CL (
  input  in_1,
  input  [15:0] in_2,
  input  CL,
  input  CLK,
  input  LD,
  output [15:0] out_6
);

  wire not_1_out, or_1_out;
  wire [15:0] controlled_buffer_1_out;

  not not_1 (not_1_out, CL);
  assign controlled_buffer_1_out = not_1_out ? in_2 : 16'bz;  // Controlled_Buffer controlled_buffer_1
  assign controlled_buffer_1_out = CL ? {16{1'b0}} : 16'bz;  // Controlled_Buffer controlled_buffer_2
  Register #(.width(16)) register_1 (.D(controlled_buffer_1_out), .en(or_1_out), .Q(out_6), .clk(CLK), .clr(in_1));
  or or_1 (or_1_out, CL, LD);
  Pull_Resistor pull_resistor_1 (.node(CL));
endmodule

module REG6_LD_INC (
  input  in_1,
  input  [5:0] in_2,
  input  in_3,
  input  CLK,
  input  LD,
  output [5:0] out_6
);

  wire not_1_out, or_1_out;
  wire [5:0] adder_1_out, controlled_buffer_1_out;

  assign controlled_buffer_1_out = in_3 ? adder_1_out : 6'bz;  // Controlled_Buffer controlled_buffer_1
  Adder #(.width(6)) adder_1 (.a(out_6), .b(6'b000001), .out(adder_1_out));  // open: cin, cout
  not not_1 (not_1_out, in_3);
  assign controlled_buffer_1_out = not_1_out ? in_2 : 6'bz;  // Controlled_Buffer controlled_buffer_2
  Register #(.width(6)) register_1 (.D(controlled_buffer_1_out), .en(or_1_out), .Q(out_6), .clk(CLK), .clr(in_1));
  or or_1 (or_1_out, in_3, LD);
  Pull_Resistor pull_resistor_1 (.node(in_3));
endmodule

module REG16_LD_INC (
  input  in_1,
  input  [15:0] in_2,
  input  in_3,
  input  CLK,
  input  LD,
  output [15:0] out_6
);

  wire not_1_out, or_1_out;
  wire [15:0] adder_1_out, controlled_buffer_1_out;

  Adder #(.width(16)) adder_1 (.a(out_6), .b(16'h1), .out(adder_1_out));  // open: cin, cout
  assign controlled_buffer_1_out = in_3 ? adder_1_out : 16'bz;  // Controlled_Buffer controlled_buffer_1
  assign controlled_buffer_1_out = not_1_out ? in_2 : 16'bz;  // Controlled_Buffer controlled_buffer_2
  not not_1 (not_1_out, in_3);
  Register #(.width(16)) register_1 (.D(controlled_buffer_1_out), .en(or_1_out), .Q(out_6), .clk(CLK), .clr(in_1));
  or or_1 (or_1_out, in_3, LD);
  Pull_Resistor pull_resistor_1 (.node(in_3));
endmodule

module REG16_LD_INC_DEC (
  input  mr,
  input  [15:0] in_2,
  input  INC,
  input  DEC,
  input  CLK,
  input  LD,
  output [15:0] out_7
);

  wire ldREG, not_1_out, not_2_out;
  wire [15:0] controlled_buffer_1_out, regDEC, regIN, regINC;

  Register #(.width(16)) register_1 (.D(regIN), .en(ldREG), .Q(out_7), .clk(CLK), .clr(mr));
  Adder #(.width(16)) adder_1 (.a(out_7), .b(16'h1), .out(regINC));  // open: cin, cout
  Subtractor #(.width(16)) subtractor_1 (.a(out_7), .b(16'h1), .out(regDEC));  // open: bin, bout
  or or_1 (ldREG, INC, DEC, LD);
  not not_1 (not_1_out, INC);
  assign controlled_buffer_1_out = INC ? regINC : 16'bz;  // Controlled_Buffer controlled_buffer_1
  not not_2 (not_2_out, DEC);
  assign regIN = not_2_out ? controlled_buffer_1_out : 16'bz;  // Controlled_Buffer controlled_buffer_2
  assign controlled_buffer_1_out = not_1_out ? in_2 : 16'bz;  // Controlled_Buffer controlled_buffer_3
  assign regIN = DEC ? regDEC : 16'bz;  // Controlled_Buffer controlled_buffer_4
  Pull_Resistor pull_resistor_1 (.node(INC));
  Pull_Resistor pull_resistor_2 (.node(DEC));

  // Other names for the same wires on the sheet: IN[15:0] = in_2; OUT[15:0] = out_7
endmodule

module MP2_6 (
  input  [5:0] I0,
  input  [5:0] I1,
  input  mx0,
  output [5:0] out_4
);

  wire not_1_out;

  not not_1 (not_1_out, mx0);
  assign out_4 = not_1_out ? I0 : 6'bz;  // Controlled_Buffer controlled_buffer_1
  assign out_4 = mx0 ? I1 : 6'bz;  // Controlled_Buffer controlled_buffer_2
endmodule

module MP2_16 (
  input  [15:0] I0,
  input  [15:0] I1,
  input  mx0,
  output [15:0] out_4
);

  wire not_1_out;

  not not_1 (not_1_out, mx0);
  assign out_4 = not_1_out ? I0 : 16'bz;  // Controlled_Buffer controlled_buffer_1
  assign out_4 = mx0 ? I1 : 16'bz;  // Controlled_Buffer controlled_buffer_2
endmodule

module MP4_16 (
  input  [15:0] I0,
  input  [15:0] I1,
  input  [15:0] I2,
  input  [15:0] I3,
  input  mx1,
  input  mx0,
  output [15:0] out_7
);

  wire and_1_out, and_2_out, and_3_out, and_4_out;

  and and_1 (and_1_out, ~mx1, ~mx0);  // AND_Gate
  and and_2 (and_2_out, ~mx1, mx0);  // AND_Gate
  and and_3 (and_3_out, mx1, ~mx0);  // AND_Gate
  and and_4 (and_4_out, mx1, mx0);
  assign out_7 = and_1_out ? I0 : 16'bz;  // Controlled_Buffer controlled_buffer_1
  assign out_7 = and_2_out ? I1 : 16'bz;  // Controlled_Buffer controlled_buffer_2
  assign out_7 = and_3_out ? I2 : 16'bz;  // Controlled_Buffer controlled_buffer_3
  assign out_7 = and_4_out ? I3 : 16'bz;  // Controlled_Buffer controlled_buffer_4
endmodule

module MP8_16 (
  input  [15:0] I0,
  input  [15:0] I1,
  input  [15:0] I2,
  input  [15:0] I3,
  input  [15:0] I4,
  input  [15:0] I5,
  input  [15:0] I6,
  input  [15:0] I6_2,
  input  mx2,
  input  mx1,
  input  mx0,
  output [15:0] out_12
);

  wire and_1_out, and_2_out, and_3_out, and_4_out, and_5_out, and_6_out, and_7_out, and_8_out;

  and and_1 (and_1_out, ~mx2, ~mx1, ~mx0);  // AND_Gate
  and and_2 (and_2_out, ~mx2, ~mx1, mx0);  // AND_Gate
  and and_3 (and_3_out, ~mx2, mx1, ~mx0);  // AND_Gate
  and and_4 (and_4_out, ~mx2, mx1, mx0);  // AND_Gate
  and and_5 (and_5_out, mx2, ~mx1, ~mx0);  // AND_Gate
  and and_6 (and_6_out, mx2, ~mx1, mx0);  // AND_Gate
  and and_7 (and_7_out, mx2, mx1, ~mx0);  // AND_Gate
  and and_8 (and_8_out, mx2, mx1, mx0);
  assign out_12 = and_1_out ? I0 : 16'bz;  // Controlled_Buffer controlled_buffer_1
  assign out_12 = and_2_out ? I1 : 16'bz;  // Controlled_Buffer controlled_buffer_2
  assign out_12 = and_3_out ? I2 : 16'bz;  // Controlled_Buffer controlled_buffer_3
  assign out_12 = and_4_out ? I3 : 16'bz;  // Controlled_Buffer controlled_buffer_4
  assign out_12 = and_5_out ? I4 : 16'bz;  // Controlled_Buffer controlled_buffer_5
  assign out_12 = and_6_out ? I5 : 16'bz;  // Controlled_Buffer controlled_buffer_6
  assign out_12 = and_7_out ? I6 : 16'bz;  // Controlled_Buffer controlled_buffer_7
  assign out_12 = and_8_out ? I6_2 : 16'bz;  // Controlled_Buffer controlled_buffer_8
endmodule

module ALU_ADD_SUB_AND (
  input  [15:0] in_1,
  input  [15:0] in_2,
  input  ADD,
  input  SUB,
  input  AND,
  output [15:0] out_6,
  output out_7
);

  wire cADD, cSUB;
  wire [15:0] ADD_t, AND_t, SUB_t;

  assign out_6 = ADD ? ADD_t : 16'bz;  // Controlled_Buffer controlled_buffer_1
  Pull_Resistor pull_resistor_1 (.node(out_6));
  Adder #(.width(16)) adder_1 (.a(in_1), .b(in_2), .out(ADD_t), .cout(cADD));  // open: cin
  Subtractor #(.width(16)) subtractor_1 (.a(in_1), .b(in_2), .out(SUB_t), .bout(cSUB));  // open: bin
  assign AND_t = in_1 & in_2;  // AND_Gate and_1, 16 bits wide
  assign out_6 = SUB ? SUB_t : 16'bz;  // Controlled_Buffer controlled_buffer_2
  assign out_6 = AND ? AND_t : 16'bz;  // Controlled_Buffer controlled_buffer_3
  assign out_7 = ADD ? cADD : 1'bz;  // Controlled_Buffer controlled_buffer_4
  Pull_Resistor pull_resistor_2 (.node(out_7));
  assign out_7 = SUB ? cSUB : 1'bz;  // Controlled_Buffer controlled_buffer_5
  Pull_Resistor pull_resistor_3 (.node(ADD));
  Pull_Resistor pull_resistor_4 (.node(SUB));
  Pull_Resistor pull_resistor_5 (.node(AND));

  // Other names for the same wires on the sheet: sADD = ADD; sAND = AND; sSUB = SUB
endmodule

module SPACE8_1 (
  input  in_1,
  input  in_2,
  input  in_3,
  input  in_4,
  input  in_5,
  input  in_6,
  input  in_7,
  input  in_8,
  output out_9,
  output out_10,
  output out_11,
  output out_12,
  output out_13,
  output out_14,
  output out_15,
  output out_16
);


  assign out_9 = in_1;
  assign out_10 = in_2;
  assign out_11 = in_3;
  assign out_12 = in_4;
  assign out_13 = in_5;
  assign out_14 = in_6;
  assign out_15 = in_7;
  assign out_16 = in_8;
endmodule

module SPACE16_1 (
  input  in_1,
  input  in_2,
  input  in_3,
  input  in_4,
  input  in_5,
  input  in_6,
  input  in_7,
  input  in_8,
  input  in_9,
  input  in_10,
  input  in_11,
  input  in_12,
  input  in_13,
  input  in_14,
  input  in_15,
  input  in_16,
  output out_17,
  output out_18,
  output out_19,
  output out_20,
  output out_21,
  output out_22,
  output out_23,
  output out_24,
  output out_25,
  output out_26,
  output out_27,
  output out_28,
  output out_29,
  output out_30,
  output out_31,
  output out_32
);


  assign out_17 = in_1;
  assign out_18 = in_2;
  assign out_19 = in_3;
  assign out_20 = in_4;
  assign out_21 = in_5;
  assign out_22 = in_6;
  assign out_23 = in_7;
  assign out_24 = in_8;
  assign out_25 = in_9;
  assign out_26 = in_10;
  assign out_27 = in_11;
  assign out_28 = in_12;
  assign out_29 = in_13;
  assign out_30 = in_14;
  assign out_31 = in_15;
  assign out_32 = in_16;
endmodule

module SPACE32_1 (
  input  in_1,
  input  in_2,
  input  in_3,
  input  in_4,
  input  in_5,
  input  in_6,
  input  in_7,
  input  in_8,
  input  in_9,
  input  in_10,
  input  in_11,
  input  in_12,
  input  in_13,
  input  in_14,
  input  in_15,
  input  in_16,
  input  in_17,
  input  in_18,
  input  in_19,
  input  in_20,
  input  in_21,
  input  in_22,
  input  in_23,
  input  in_24,
  input  in_25,
  input  in_26,
  input  in_27,
  input  in_28,
  input  in_29,
  input  in_30,
  input  in_31,
  input  in_32,
  output out_33,
  output out_34,
  output out_35,
  output out_36,
  output out_37,
  output out_38,
  output out_39,
  output out_40,
  output out_41,
  output out_42,
  output out_43,
  output out_44,
  output out_45,
  output out_46,
  output out_47,
  output out_48,
  output out_49,
  output out_50,
  output out_51,
  output out_52,
  output out_53,
  output out_54,
  output out_55,
  output out_56,
  output out_57,
  output out_58,
  output out_59,
  output out_60,
  output out_61,
  output out_62,
  output out_63,
  output out_64
);


  assign out_33 = in_1;
  assign out_34 = in_2;
  assign out_35 = in_3;
  assign out_36 = in_4;
  assign out_37 = in_5;
  assign out_38 = in_6;
  assign out_39 = in_7;
  assign out_40 = in_8;
  assign out_41 = in_9;
  assign out_42 = in_10;
  assign out_43 = in_11;
  assign out_44 = in_12;
  assign out_45 = in_13;
  assign out_46 = in_14;
  assign out_47 = in_15;
  assign out_48 = in_16;
  assign out_49 = in_17;
  assign out_50 = in_18;
  assign out_51 = in_19;
  assign out_52 = in_20;
  assign out_53 = in_21;
  assign out_54 = in_22;
  assign out_55 = in_23;
  assign out_56 = in_24;
  assign out_57 = in_25;
  assign out_58 = in_26;
  assign out_59 = in_27;
  assign out_60 = in_28;
  assign out_61 = in_29;
  assign out_62 = in_30;
  assign out_63 = in_31;
  assign out_64 = in_32;
endmodule

module SPACE_INV32_1 (
  input  in_1,
  input  in_2,
  input  in_3,
  input  in_4,
  input  in_5,
  input  in_6,
  input  in_7,
  input  in_8,
  input  in_9,
  input  in_10,
  input  in_11,
  input  in_12,
  input  in_13,
  input  in_14,
  input  in_15,
  input  in_16,
  input  in_17,
  input  in_18,
  input  in_19,
  input  in_20,
  input  in_21,
  input  in_22,
  input  in_23,
  input  in_24,
  input  in_25,
  input  in_26,
  input  in_27,
  input  in_28,
  input  in_29,
  input  in_30,
  input  in_31,
  input  in_32,
  output out_33,
  output out_34,
  output out_35,
  output out_36,
  output out_37,
  output out_38,
  output out_39,
  output out_40,
  output out_41,
  output out_42,
  output out_43,
  output out_44,
  output out_45,
  output out_46,
  output out_47,
  output out_48,
  output out_49,
  output out_50,
  output out_51,
  output out_52,
  output out_53,
  output out_54,
  output out_55,
  output out_56,
  output out_57,
  output out_58,
  output out_59,
  output out_60,
  output out_61,
  output out_62,
  output out_63,
  output out_64
);


  assign out_33 = in_1;
  assign out_34 = in_2;
  assign out_35 = in_3;
  assign out_36 = in_4;
  assign out_37 = in_5;
  assign out_38 = in_6;
  assign out_39 = in_7;
  assign out_40 = in_8;
  assign out_41 = in_9;
  assign out_42 = in_10;
  assign out_43 = in_11;
  assign out_44 = in_12;
  assign out_45 = in_13;
  assign out_46 = in_14;
  assign out_47 = in_15;
  assign out_48 = in_16;
  assign out_49 = in_17;
  assign out_50 = in_18;
  assign out_51 = in_19;
  assign out_52 = in_20;
  assign out_53 = in_21;
  assign out_54 = in_22;
  assign out_55 = in_23;
  assign out_56 = in_24;
  assign out_57 = in_25;
  assign out_58 = in_26;
  assign out_59 = in_27;
  assign out_60 = in_28;
  assign out_61 = in_29;
  assign out_62 = in_30;
  assign out_63 = in_31;
  assign out_64 = in_32;
endmodule

module SPACE_INV16_1 (
  input  in_1,
  input  in_2,
  input  in_3,
  input  in_4,
  input  in_5,
  input  in_6,
  input  in_7,
  input  in_8,
  input  in_9,
  input  in_10,
  input  in_11,
  input  in_12,
  input  in_13,
  input  in_14,
  input  in_15,
  input  in_16,
  output out_17,
  output out_18,
  output out_19,
  output out_20,
  output out_21,
  output out_22,
  output out_23,
  output out_24,
  output out_25,
  output out_26,
  output out_27,
  output out_28,
  output out_29,
  output out_30,
  output out_31,
  output out_32
);


  assign out_17 = in_1;
  assign out_18 = in_2;
  assign out_19 = in_3;
  assign out_20 = in_4;
  assign out_21 = in_5;
  assign out_22 = in_6;
  assign out_23 = in_7;
  assign out_24 = in_8;
  assign out_25 = in_9;
  assign out_26 = in_10;
  assign out_27 = in_11;
  assign out_28 = in_12;
  assign out_29 = in_13;
  assign out_30 = in_14;
  assign out_31 = in_15;
  assign out_32 = in_16;
endmodule

module SPACE_INV8_1 (
  input  in_1,
  input  in_2,
  input  in_3,
  input  in_4,
  input  in_5,
  input  in_6,
  input  in_7,
  input  in_8,
  output out_9,
  output out_10,
  output out_11,
  output out_12,
  output out_13,
  output out_14,
  output out_15,
  output out_16
);


  assign out_9 = in_1;
  assign out_10 = in_2;
  assign out_11 = in_3;
  assign out_12 = in_4;
  assign out_13 = in_5;
  assign out_14 = in_6;
  assign out_15 = in_7;
  assign out_16 = in_8;
endmodule
