// Logisim project ORT2Project.circ as structural Verilog: 8 circuits, main circuit COMPUTER
module COMPUTER (
);

  wire BTN_RST_out, CLK, cpu_1_inta, interrupt_interface_8_1_p4, interrupt_interface_8_1_p5,
       interrupt_interface_8_1_p6, interrupt_interface_8_1_p7, interrupt_interface_8_1_p8,
       interrupt_interface_8_1_p9, interrupt_interface_8_1_p10, interrupt_interface_8_1_p11,
       pull_resistor_4_node, pull_resistor_5_node, ram_1_out_8, rst;
  wire [2:0] cpu_1_uext1__0;
  wire [7:0] interrupt_interface_8_1_p1;
  wire [15:0] pull_resistor_1_node, pull_resistor_3_node, ram_1_out_7;

  Button BTN_RST (.out(BTN_RST_out));
  Clock u_CLK (.out(CLK));
  // RisingEdge risingedge_1: pin names not known; wires that end beside it: BTN_RST_out, CLK, rst
  RAM ram_1 (
    .in_1(pull_resistor_1_node), .in_2(CLK), .in_3(pull_resistor_3_node), .in_4(pull_resistor_4_node),
    .in_5(pull_resistor_5_node), .in_6(rst), .out_7(ram_1_out_7), .out_8(ram_1_out_8));
  Pull_Resistor pull_resistor_1 (.node(pull_resistor_1_node));
  Pull_Resistor pull_resistor_2 (.node(ram_1_out_7));
  Pull_Resistor pull_resistor_3 (.node(pull_resistor_3_node));
  Pull_Resistor pull_resistor_4 (.node(pull_resistor_4_node));
  Pull_Resistor pull_resistor_5 (.node(pull_resistor_5_node));
  Pull_Resistor pull_resistor_6 (.node(ram_1_out_8));
  CPU cpu_1 (
    .in_1(rst), .in_2(CLK), .in_3(ram_1_out_8), .in_4(ram_1_out_7), .ABUS(pull_resistor_1_node),
    .DOUTBUS(pull_resistor_3_node), .out_8(pull_resistor_4_node), .out_9(pull_resistor_5_node),
    .inta(cpu_1_inta), .intr3__0(interrupt_interface_8_1_p1), .UEXT1__0(cpu_1_uext1__0));
  // INTERRUPT_INTERFACE_8 interrupt_interface_8_1: pin names not known; wires that end beside it: interrupt_interface_8_1_p1, cpu_1_inta, cpu_1_uext1__0, interrupt_interface_8_1_p4, interrupt_interface_8_1_p5, interrupt_interface_8_1_p6, interrupt_interface_8_1_p7, interrupt_interface_8_1_p8, interrupt_interface_8_1_p9, interrupt_interface_8_1_p10, interrupt_interface_8_1_p11, CLK
  Button BTN_INTR7 (.out(interrupt_interface_8_1_p4));
  Button BTN_INTR6 (.out(interrupt_interface_8_1_p5));
  Button BTN_INTR5 (.out(interrupt_interface_8_1_p6));
  Button BTN_INTR4 (.out(interrupt_interface_8_1_p7));
  Button BTN_INTR3 (.out(interrupt_interface_8_1_p8));
  Button BTN_INTR2 (.out(interrupt_interface_8_1_p9));
  Button BTN_INTR1 (.out(interrupt_interface_8_1_p10));
  Button BTN_INTR0 (.out(interrupt_interface_8_1_p11));
endmodule

module CPU (
  input  in_1,
  input  in_2,
  input  in_3,
  input  [15:0] in_4,
  input  [7:0] intr3__0,
  output [15:0] ABUS,
  output [15:0] DOUTBUS,
  output out_8,
  output out_9,
  output inta,
  output [2:0] UEXT1__0
);

  wire [3:0] common_1_phaseffbus;
  wire [6:0] common_1_addrbus, pull_resistor_2_node;
  wire [7:0] pull_resistor_5_node;
  wire [8:0] pull_resistor_6_node;
  wire [15:0] A, B, INTRADDR, PSW;
  wire [16:0] ALU;
  wire [20:0] common_1_instrucbus;
  wire [31:0] pull_resistor_4_node;

  COMMON common_1 (
    .CLK(in_2), .RST(in_1), .DIN(in_4), .CMEMBUS(pull_resistor_4_node), .MAR(ABUS), .MDR(DOUTBUS),
    .PHASEFFBUS(common_1_phaseffbus), .INSTRUCBUS(common_1_instrucbus), .ADDRBUS(common_1_addrbus),
    .PSW(PSW), .CREGBUS(pull_resistor_6_node), .CFFBUS(pull_resistor_5_node), .B(B), .A(A),
    .CPSW(pull_resistor_2_node), .ALU(ALU), .IVTPPDSP(INTRADDR));
  Pull_Resistor pull_resistor_1 (.node(common_1_phaseffbus));
  Pull_Resistor pull_resistor_2 (.node(pull_resistor_2_node));
  Pull_Resistor pull_resistor_3 (.node(common_1_instrucbus));
  Pull_Resistor pull_resistor_4 (.node(pull_resistor_4_node));
  Pull_Resistor pull_resistor_5 (.node(pull_resistor_5_node));
  Pull_Resistor pull_resistor_6 (.node(pull_resistor_6_node));
  Pull_Resistor pull_resistor_7 (.node(common_1_addrbus));
  FETCH fetch_1 (
    .in_1(in_1), .in_2(in_2), .in_3(in_3), .PHASEFFBUS(common_1_phaseffbus),
    .INSTRUCBUS(common_1_instrucbus), .ADDRBUS(common_1_addrbus), .PSW(PSW), .rdMEM(out_9),
    .CMEMBUS(pull_resistor_4_node), .CFFBUS(pull_resistor_5_node), .CREGBUS(pull_resistor_6_node));
  ADDR addr_1 (
    .in_1(in_1), .in_2(in_2), .in_3(in_3), .PHASEFFBUS(common_1_phaseffbus),
    .INSTRUCBUS(common_1_instrucbus), .ADDRBUS(common_1_addrbus), .rdMEM(out_9),
    .CMEMBUS(pull_resistor_4_node), .CFFBUS(pull_resistor_5_node), .CREGBUS(pull_resistor_6_node));
  EXEC exec_1 (
    .in_1(in_1), .in_2(in_2), .in_3(in_3), .B(B), .PHASEFFBUS(common_1_phaseffbus),
    .INSTRUCBUS(common_1_instrucbus), .ADDRBUS(common_1_addrbus), .PSW(PSW), .A(A), .ALU(ALU),
    .CMEMBUS(pull_resistor_4_node), .CFFBUS(pull_resistor_5_node), .CREGBUS(pull_resistor_6_node),
    .CPSW(pull_resistor_2_node), .rdMEM(out_9), .wrMEM(out_8), .in_5(DOUTBUS));
  INTR intr_1 (
    .in_1(in_1), .in_2(in_2), .in_3(in_3), .PHASEFFBUS(common_1_phaseffbus),
    .INSTRUCBUS(common_1_instrucbus), .PSW(PSW), .intr(intr3__0), .ADDIVTP(INTRADDR),
    .CMEMBUS(pull_resistor_4_node), .CFFBUS(pull_resistor_5_node), .CREGBUS(pull_resistor_6_node),
    .rdMEM(out_9), .wrMEM(out_8), .UEXT1__0(UEXT1__0), .inta(inta));

  // Other names for the same wires on the sheet: CLK = in_2; DIN15__0[15:0] = in_4; FCBUS = in_3; MAR[15:0] = ABUS;
  //   MDR[15:0] = DOUTBUS; RD = out_9; rst = in_1; WR = out_8
endmodule

module COMMON (
  input  CLK,
  input  RST,
  input  [15:0] DIN,
  input  [15:0] A,
  input  [16:0] ALU,
  input  [15:0] IVTPPDSP,
  input  [31:0] CMEMBUS,
  input  [7:0] CFFBUS,
  input  [8:0] CREGBUS,
  input  [6:0] CPSW,
  output [15:0] MAR,
  output [15:0] MDR,
  output [3:0] PHASEFFBUS,
  output [20:0] INSTRUCBUS,
  output [6:0] ADDRBUS,
  output [15:0] PSW,
  output [15:0] B
);

  wire addr_inst, and_7_out, and_8_out, and_9_out, and_10_out, and_11_out, and_12_out, and_13_out,
       and_14_out, and_15_out, and_16_out, and_17_out, and_18_out, and_19_out, and_20_out, and_21_out,
       and_22_out, and_23_out, and_24_out, and_25_out, and_26_out, and_27_out, and_28_out, and_29_out,
       and_30_out, and_31_out, and_32_out, and_33_out, and_34_out, and_35_out, bezaddr_inst, bz_jmp_inst,
       C_p4, clADDR, clDR, clEXEC, clFETCH, clINTR, clMDR, clPSWSTART, comparator_1_eq, comparator_2_eq,
       decSP, grinst1, grinst2, grinst3, grinst4, grinst5, grinst6, I_p4, incB, incDW, incMAR, incPC, incSP,
       ldAR, ldB, ldBR0, ldBR1, ldC, ldDR, ldDW, ldI, ldIR15__0, ldIR31__16, ldMAR, ldMDR, ldN, ldPC, ldS,
       ldSP, ldV, ldXR0, ldXR1, ldZ, mp2_16b_3_p3, mp2_16b_4_p3, mxADD00, mxADD01, mxADD10, mxADD11, mxB0,
       mxB1, mxB2, mxMAR0, mxMAR1, mxMAR2, mxMDR0, mxMDR1, mxPC0, mxPC1, mxSP0, mxSP1, nor_1_out, nor_2_out,
       nor_3_out, nor_4_out, nor_5_out, not_1_out, not_4_out, or_2_out, or_3_out, or_4_out, or_5_out,
       or_6_out, or_7_out, or_8_out, or_9_out, or_10_out, or_11_out, or_12_out, or_13_out, rsff_2_p4,
       rsff_3_p4, rsff_4_p4, stADDR, stEXEC, stFETCH, stINTR, usl_jmp_inst, V_p4, Z_p4;
  wire [3:0] IR27__24;
  wire [7:0] IR7__0, IR23__16;
  wire [15:0] add16_1_p3, ADDW, AR, bit_extender_1_out, BR, BR0, BR1, BR_XR, DR, DW, mp2_16_1_out_4,
       mp4_16_1_out_7, mp4_16_2_out_7, mp4_16_4_out_7, mp4_16_5_out_7, mp8_16_1_out_12, mp8_16_2_out_12, PC,
       SP, XR, XR0, XR1;
  wire [15:8] IR15__0;
  wire [15:12] IR31__16;

  SPACE_INV32_1 space_inv32_1_1 (
    .in_1(CMEMBUS[31]), .in_2(CMEMBUS[30]), .in_3(CMEMBUS[29]), .in_4(CMEMBUS[28]), .in_5(CMEMBUS[27]),
    .in_6(CMEMBUS[26]), .in_7(CMEMBUS[25]), .in_8(CMEMBUS[24]), .in_9(CMEMBUS[23]), .in_10(CMEMBUS[22]),
    .in_11(CMEMBUS[21]), .in_12(CMEMBUS[20]), .in_13(CMEMBUS[19]), .in_14(CMEMBUS[18]), .in_15(CMEMBUS[17]),
    .in_16(CMEMBUS[16]), .in_17(CMEMBUS[15]), .in_18(CMEMBUS[14]), .in_19(CMEMBUS[13]), .in_20(CMEMBUS[12]),
    .in_21(CMEMBUS[11]), .in_22(CMEMBUS[10]), .in_23(CMEMBUS[9]), .in_24(CMEMBUS[8]), .in_25(CMEMBUS[7]),
    .in_26(CMEMBUS[6]), .in_27(CMEMBUS[5]), .in_28(CMEMBUS[4]), .in_29(CMEMBUS[3]), .in_30(CMEMBUS[2]),
    .in_31(CMEMBUS[1]), .in_32(CMEMBUS[0]), .out_33(decSP), .out_34(mxSP0), .out_35(mxSP1), .out_36(clDR),
    .out_37(mxB2), .out_38(clMDR), .out_39(mxMDR0), .out_40(mxMDR1), .out_41(mxMAR2), .out_42(mxPC0),
    .out_43(mxPC1), .out_44(ldXR1), .out_45(ldXR0), .out_46(ldBR1), .out_47(ldBR0), .out_48(incB),
    .out_49(ldAR), .out_50(ldDR), .out_51(mxADD11), .out_52(mxADD10), .out_53(mxADD01), .out_54(mxADD00),
    .out_55(mxMAR0), .out_56(mxMAR1), .out_57(mxB1), .out_58(mxB0), .out_59(ldB), .out_60(incPC),
    .out_61(ldPC), .out_62(ldMDR), .out_63(incMAR), .out_64(ldMAR));
  SPACE_INV8_1 space_inv8_1_1 (
    .in_1(CFFBUS[7]), .in_2(CFFBUS[6]), .in_3(CFFBUS[5]), .in_4(CFFBUS[4]), .in_5(CFFBUS[3]),
    .in_6(CFFBUS[2]), .in_7(CFFBUS[1]), .in_8(CFFBUS[0]), .out_9(clINTR), .out_10(stINTR), .out_11(clEXEC),
    .out_12(stEXEC), .out_13(clADDR), .out_14(stADDR), .out_15(clFETCH), .out_16(stFETCH));
  SPACE_INV8_1 space_inv8_1_2 (
    .in_1(CREGBUS[7]), .in_2(CREGBUS[6]), .in_3(CREGBUS[5]), .in_4(CREGBUS[4]), .in_5(CREGBUS[3]),
    .in_6(CREGBUS[2]), .in_7(CREGBUS[1]), .in_8(CREGBUS[0]), .out_11(ldIR31__16), .out_12(ldIR15__0),
    .out_13(incDW), .out_14(ldDW), .out_15(incSP), .out_16(ldSP));  // open: out_9, out_10
  SPACE_INV8_1 space_inv8_1_3 (
    .in_2(CPSW[6]), .in_3(CPSW[5]), .in_4(CPSW[4]), .in_5(CPSW[3]), .in_6(CPSW[2]), .in_7(CPSW[1]),
    .in_8(CPSW[0]), .out_10(ldS), .out_11(ldI), .out_12(ldZ), .out_13(ldN), .out_14(ldC), .out_15(ldV),
    .out_16(clPSWSTART));  // open: in_1, out_9
  MP8_16 mp8_16_1 (
    .mx2(mxMAR2), .mx1(mxMAR1), .mx0(mxMAR0), .I0(PC), .I1({IR15__0, IR7__0}), .I2(AR), .I3(ADDW), .I4(SP),
    .I5(DW), .I6(B), .I6_2(IVTPPDSP), .out_12(mp8_16_1_out_12));
  // REG16_LD reg16_ld_1: pin names not known; wires that end beside it: CLK, A, BR0, ldBR0
  REG16_LD_INC reg16_ld_inc_1 (
    .CLK(CLK), .in_3(incMAR), .LD(ldMAR), .in_2(mp8_16_1_out_12), .out_6(MAR));  // open: in_1
  REG16_LD reg16_ld_2 (.CLK(CLK), .LD(ldIR31__16), .in_2(MDR), .out_5({IR31__16, IR27__24, IR23__16}));  // open: in_1
  // DC4_16 dc4_16_1: pin names not known; wires that end beside it: IR31__16, PSW[0], addr_inst, bz_jmp_inst, bezaddr_inst, usl_jmp_inst
  // DC4_16 dc4_16_2: pin names not known; wires that end beside it: IR27__24, addr_inst, INSTRUCBUS[13], INSTRUCBUS[14], INSTRUCBUS[15], INSTRUCBUS[16], INSTRUCBUS[17], INSTRUCBUS[18], INSTRUCBUS[19]
  // MP2_16b mp2_16b_1: pin names not known; wires that end beside it: IR23__16[0], BR0, BR, BR1, 1'b1
  nor nor_1 (nor_1_out, INSTRUCBUS[13], INSTRUCBUS[14], INSTRUCBUS[15], INSTRUCBUS[16], INSTRUCBUS[17], INSTRUCBUS[18], INSTRUCBUS[19]);
  nor nor_2 (nor_2_out, ADDRBUS[0], ADDRBUS[1], ADDRBUS[2], ADDRBUS[3], ADDRBUS[4], ADDRBUS[5], ADDRBUS[6]);
  MP4_16 mp4_16_1 (.mx1(mxADD01), .mx0(mxADD00), .I0(BR), .I1(XR), .I2(BR_XR), .out_7(mp4_16_1_out_7));  // open: I3
  and and_1 (grinst5, addr_inst, nor_1_out);
  and and_2 (grinst6, addr_inst, nor_2_out);
  // REG16_LD reg16_ld_3: pin names not known; wires that end beside it: CLK, A, BR1, ldBR1
  // ADD16 add16_1: pin names not known; wires that end beside it: mp4_16_1_out_7, ADDW, add16_1_p3, IR15__0
  REG16_LD_CL reg16_ld_cl_1 (.CLK(CLK), .CL(clMDR), .LD(ldMDR), .in_2(mp4_16_2_out_7), .out_6(MDR));  // open: in_1
  REG16_LD reg16_ld_4 (.CLK(CLK), .LD(ldIR15__0), .in_2(MDR), .out_5({IR15__0, IR7__0}));  // open: in_1
  // DC4_16 dc4_16_3: pin names not known; wires that end beside it: IR27__24, bezaddr_inst, INSTRUCBUS[0], INSTRUCBUS[1], INSTRUCBUS[2], INSTRUCBUS[3], INSTRUCBUS[4], INSTRUCBUS[5], INSTRUCBUS[6], INSTRUCBUS[7], INSTRUCBUS[8]
  // DC4_16 dc4_16_4: pin names not known; wires that end beside it: IR23__16[7:4], addr_inst, ADDRBUS[0], ADDRBUS[1], ADDRBUS[2], ADDRBUS[3], ADDRBUS[4], ADDRBUS[5], ADDRBUS[6]
  // REG16_LD reg16_ld_5: pin names not known; wires that end beside it: CLK, A, XR0, ldXR0
  assign bit_extender_1_out = {{8{IR15__0[15]}}, IR15__0};  // Bit_Extender bit_extender_1
  MP4_16 mp4_16_2 (.mx1(mxMDR1), .mx0(mxMDR0), .I0(DIN), .I1(A), .I2(PC), .I3(PSW), .out_7(mp4_16_2_out_7));
  or or_1 (INSTRUCBUS[20], grinst1, grinst2, grinst3, grinst4, grinst5, grinst6);
  // MP2_16b mp2_16b_2: pin names not known; wires that end beside it: IR23__16[0], XR0, XR, XR1, 1'b1
  MP4_16 mp4_16_3 (.mx1(mxADD11), .mx0(mxADD10), .I0(bit_extender_1_out), .out_7(add16_1_p3));  // open: I1, I2, I3
  // DC4_16 dc4_16_5: pin names not known; wires that end beside it: IR27__24, usl_jmp_inst, INSTRUCBUS[9], INSTRUCBUS[10], INSTRUCBUS[11]
  // REG16_LD reg16_ld_6: pin names not known; wires that end beside it: CLK, A, XR1, ldXR1
  // MP2_16b mp2_16b_3: pin names not known; wires that end beside it: IR23__16[0], BR0, mp2_16b_3_p3, BR1, 1'b1
  not not_1 (not_1_out, RST);
  // RSFF rsff_1: pin names not known; wires that end beside it: clFETCH, CLK, stFETCH, not_1_out, PHASEFFBUS[0]
  MP4_16 mp4_16_4 (
    .mx1(mxPC1), .mx0(mxPC0), .I0(MDR), .I1({IR15__0, IR7__0}), .I2(B), .out_7(mp4_16_4_out_7));  // open: I3
  MP2_16 mp2_16_1 (.mx0(RST), .I0(mp4_16_4_out_7), .I1(16'h1000), .out_4(mp2_16_1_out_4));
  REG16_LD_INC reg16_ld_inc_2 (
    .CLK(CLK), .in_3(incPC), .LD(or_2_out), .in_2(mp2_16_1_out_4), .out_6(PC));  // open: in_1
  // DC4_16 dc4_16_6: pin names not known; wires that end beside it: IR27__24, bz_jmp_inst, INSTRUCBUS[12]
  nor nor_3 (nor_3_out, addr_inst, bz_jmp_inst, bezaddr_inst, usl_jmp_inst);
  nor nor_4 (nor_4_out, INSTRUCBUS[0], INSTRUCBUS[1], INSTRUCBUS[2], INSTRUCBUS[3], INSTRUCBUS[4], INSTRUCBUS[5], INSTRUCBUS[6], INSTRUCBUS[7], INSTRUCBUS[8]);
  nor nor_5 (nor_5_out, INSTRUCBUS[9], INSTRUCBUS[10], INSTRUCBUS[11]);
  // MP2_16b mp2_16b_4: pin names not known; wires that end beside it: IR23__16[0], XR0, mp2_16b_4_p3, XR1, 1'b1
  // ADD16 add16_2: pin names not known; wires that end beside it: mp2_16b_3_p3, BR_XR, mp2_16b_4_p3
  or or_2 (or_2_out, ldPC, RST);
  and and_3 (grinst1, PSW[0], nor_3_out);
  and and_4 (grinst2, bezaddr_inst, nor_4_out);
  and and_5 (grinst3, usl_jmp_inst, nor_5_out);
  and and_6 (grinst4, bz_jmp_inst, ~INSTRUCBUS[12]);  // AND_Gate
  REG16_LD_CL reg16_ld_cl_2 (.CLK(CLK), .CL(clDR), .LD(ldDR), .in_2(A), .out_6(DR));  // open: in_1
  // REG16_LD reg16_ld_7: pin names not known; wires that end beside it: CLK, A, AR, ldAR
  // RSFF rsff_2: pin names not known; wires that end beside it: clADDR, CLK, stADDR, rsff_2_p4, PHASEFFBUS[1]
  not not_2 (rsff_2_p4, RST);
  and and_7 (and_7_out, INSTRUCBUS[2], ldS, ~MDR[0]);  // AND_Gate
  and and_8 (and_8_out, INSTRUCBUS[2], ldS, MDR[0]);
  and and_9 (and_9_out, A[15], B[15], ~ALU[15]);  // AND_Gate
  or or_3 (or_3_out, and_9_out, and_10_out);
  and and_10 (and_10_out, ~A[15], ~B[15], ALU[15]);  // AND_Gate
  and and_11 (and_11_out, A[15], ~B[15], ~ALU[15]);  // AND_Gate
  or or_4 (or_4_out, and_11_out, and_12_out);
  and and_12 (and_12_out, ~A[15], B[15], ALU[15]);  // AND_Gate
  or or_5 (or_5_out, INSTRUCBUS[16], INSTRUCBUS[15], INSTRUCBUS[13]);
  Comparator #(.width(16)) comparator_1 (.a(A), .b({16{1'b0}}), .eq(comparator_1_eq));  // open: gt, lt
  Comparator #(.width(16)) comparator_2 (.a(ALU[15:0]), .b({16{1'b0}}), .eq(comparator_2_eq));  // open: gt, lt
  MP8_16 mp8_16_2 (
    .mx2(mxB2), .mx1(mxB1), .mx0(mxB0), .I0(MDR), .I1({IR15__0, IR7__0}), .I2(DR), .I3(ADDW), .I4(BR1),
    .out_12(mp8_16_2_out_12));  // open: I5, I6, I6_2
  // RSFF rsff_3: pin names not known; wires that end beside it: clEXEC, CLK, stEXEC, rsff_3_p4, PHASEFFBUS[2]
  not not_3 (rsff_3_p4, RST);
  and and_13 (and_13_out, MDR[1], INSTRUCBUS[2]);
  and and_14 (and_14_out, INSTRUCBUS[16], or_3_out);
  or or_6 (or_6_out, and_14_out, and_15_out);
  and and_15 (and_15_out, INSTRUCBUS[17], or_4_out);
  and and_16 (and_16_out, MDR[3], INSTRUCBUS[2]);
  and and_17 (and_17_out, or_5_out, comparator_1_eq);
  and and_18 (and_18_out, INSTRUCBUS[17], comparator_2_eq);
  and and_19 (and_19_out, MDR[4], INSTRUCBUS[2]);
  or or_7 (or_7_out, INSTRUCBUS[16], INSTRUCBUS[15], INSTRUCBUS[13]);
  and and_20 (and_20_out, or_7_out, A[15]);
  and and_21 (and_21_out, INSTRUCBUS[17], ALU[15]);
  REG16_LD_INC reg16_ld_inc_3 (.CLK(CLK), .in_3(incB), .LD(ldB), .in_2(mp8_16_2_out_12), .out_6(B));  // open: in_1
  REG16_LD_INC_DEC reg16_ld_inc_dec_1 (
    .CLK(CLK), .INC(incSP), .DEC(decSP), .LD(or_13_out), .in_2(mp4_16_5_out_7), .out_7(SP));  // open: mr
  or or_8 (or_8_out, clPSWSTART, and_7_out);
  or or_9 (or_9_out, and_13_out, or_6_out);
  and and_22 (and_22_out, MDR[2], INSTRUCBUS[2]);
  and and_23 (and_23_out, ALU[16], INSTRUCBUS[16]);
  or or_10 (or_10_out, and_23_out, and_22_out, and_24_out);
  and and_24 (and_24_out, ALU[16], INSTRUCBUS[17]);
  or or_11 (or_11_out, and_16_out, and_18_out, and_17_out);
  or or_12 (or_12_out, and_19_out, and_21_out, and_20_out);
  and and_25 (and_25_out, MDR[15], INSTRUCBUS[2]);
  MP4_16 mp4_16_5 (.mx1(mxSP1), .mx0(mxSP0), .I0(16'hf000), .out_7(mp4_16_5_out_7));  // open: I1, I2, I3
  not not_4 (not_4_out, RST);
  // RSFF S: pin names not known; wires that end beside it: or_8_out, CLK, and_8_out, not_4_out, PSW[0]
  or or_13 (or_13_out, RST, ldSP);
  // RSFF rsff_4: pin names not known; wires that end beside it: clINTR, CLK, stINTR, rsff_4_p4, PHASEFFBUS[3]
  not not_5 (rsff_4_p4, RST);
  and and_26 (and_26_out, ~or_9_out, ldV);  // AND_Gate
  and and_27 (and_27_out, or_9_out, ldV);
  and and_28 (and_28_out, ~or_10_out, ldC);  // AND_Gate
  and and_29 (and_29_out, or_10_out, ldC);
  and and_30 (and_30_out, ~or_11_out, ldZ);  // AND_Gate
  and and_31 (and_31_out, or_11_out, ldZ);
  and and_32 (and_32_out, ~or_12_out, ldN);  // AND_Gate
  and and_33 (and_33_out, or_12_out, ldN);
  and and_34 (and_34_out, ~and_25_out, ldI);  // AND_Gate
  and and_35 (and_35_out, and_25_out, ldI);
  REG16_LD_INC reg16_ld_inc_4 (.CLK(CLK), .in_3(incDW), .LD(ldDW), .in_2(BR0), .out_6(DW));  // open: in_1
  // RSFF V: pin names not known; wires that end beside it: and_26_out, CLK, and_27_out, V_p4, PSW[1]
  not not_6 (V_p4, RST);
  // RSFF C: pin names not known; wires that end beside it: and_28_out, CLK, and_29_out, C_p4, PSW[2]
  not not_7 (C_p4, RST);
  // RSFF Z: pin names not known; wires that end beside it: and_30_out, CLK, and_31_out, Z_p4, PSW[3]
  not not_8 (Z_p4, RST);
  // RSFF N: pin names not known; wires that end beside it: and_32_out, CLK, and_33_out, PSW[4]
  // NOT_Gate not_9 has open pins: in=RST, out=open
  // RSFF I: pin names not known; wires that end beside it: and_34_out, CLK, and_35_out, I_p4, PSW[15]
  not not_10 (I_p4, RST);
  Pull_Resistor pull_resistor_1 (.node(PSW));

  // Other names for the same wires on the sheet: immed = ADDRBUS[0]; memdir = ADDRBUS[1]; regdir = ADDRBUS[2];
  //   regind = ADDRBUS[3]; brpom = ADDRBUS[4]; xrpom = ADDRBUS[5]; bxpom = ADDRBUS[6]; ALU_t[15:0] = ALU[15:0];
  //   Din15__0[15:0] = DIN; ENTRADDR15__0[15:0] = IVTPPDSP; HALT = INSTRUCBUS[0]; RTS = INSTRUCBUS[1];
  //   RTI = INSTRUCBUS[2]; STBR0 = INSTRUCBUS[3]; STXR0 = INSTRUCBUS[4]; STBR1 = INSTRUCBUS[5]; STXR1 = INSTRUCBUS[6];
  //   STRCPY = INSTRUCBUS[7]; STAR = INSTRUCBUS[8]; ЈNEQ = INSTRUCBUS[9]; ЈLSSU = INSTRUCBUS[10];
  //   JLSS = INSTRUCBUS[11]; JMP = INSTRUCBUS[12]; LD = INSTRUCBUS[13]; ST = INSTRUCBUS[14]; AND = INSTRUCBUS[15];
  //   ADD = INSTRUCBUS[16]; CMP = INSTRUCBUS[17]; JSR = INSTRUCBUS[18]; CLR = INSTRUCBUS[19]; grinst = INSTRUCBUS[20];
  //   IR15__0[7:0] = IR7__0; IR15__8[7:0] = IR15__0; IR31__16[11:0] = {IR27__24, IR23__16};
  //   IR31__24[7:0] = {IR31__16, IR27__24}; MAR15__0[15:0] = MAR; MDR15__0[15:0] = MDR; PC15__0[15:0] = PC;
  //   FETCH = PHASEFFBUS[0]; ADDR = PHASEFFBUS[1]; EXEC = PHASEFFBUS[2]; INTR = PHASEFFBUS[3]; PSWSTART = PSW[0];
  //   PSWV = PSW[1]; PSWC = PSW[2]; PSWZ = PSW[3]; PSWN = PSW[4]; PSWI = PSW[15]

  // Notes on the sheet:
  //   Instrukcijski registar
  //   Sabirac
  //   MAR
  //   Registri BR, XR, DR, AR
  //   Dekoderi za prepoznavanje instrukcije na osnovu sadrzaja registra IR31..24
  //   MDR
  //   PC
  //   FF za pokretanje FETCH, ADDR, EXEC i INTR faze izvršavanja instrukcije
  //   Registar SP
  //   Registar B
  //   Programska statusna reč (PSW)
  //   Registar DW
endmodule

module FETCH (
  input  in_1,
  input  in_2,
  input  in_3,
  input  [3:0] PHASEFFBUS,
  input  [20:0] INSTRUCBUS,
  input  [6:0] ADDRBUS,
  input  [15:0] PSW,
  output [31:0] CMEMBUS,
  output [8:0] CREGBUS,
  output [7:0] CFFBUS,
  output rdMEM
);

  wire adr2, and_2_out, and_3_out, and_4_out, and_5_out, and_6_out, and_7_out, bezadr2, bradr2, brbezadr2,
       brcnd, brgrinst, brjmp4, brnotFCBUS, brnotPSWSTandFETCH, bruncnd, clADDR, clDR, clEXEC, clFETCH,
       clINTR, clMDR, decSP, incB, incDW, incMAR, incPC, incSP, jmp4, ldAR, ldB, ldBR0, ldBR1, ldDR, ldDW,
       ldIR15__0, ldIR31__16, ldMAR, ldMDR, ldPC, ldSP, ldXR0, ldXR1, mxADD00, mxADD01, mxADD10, mxADD11,
       mxB0, mxB1, mxB2, mxMAR0, mxMAR1, mxMAR2, mxMDR0, mxMDR1, mxPC0, mxPC1, mxSP0, mxSP1, not_1_out,
       not_3_out, not_4_out, or_3_out, or_4_out, or_6_out, rdMEM_t, reg4_inc_ld_1_p5, reg4_inc_ld_1_p6,
       space8_1_1_out_9, space8_1_1_out_10, space8_1_1_out_11, space8_1_1_out_12, space8_1_1_out_13,
       space8_1_1_out_14, space8_1_1_out_15, space8_1_1_out_16, space8_1_2_out_9, space8_1_2_out_10,
       space8_1_2_out_11, space8_1_2_out_12, space8_1_2_out_13, space8_1_2_out_14, space8_1_2_out_15,
       space8_1_2_out_16, space32_1_1_out_33, space32_1_1_out_34, space32_1_1_out_35, space32_1_1_out_36,
       space32_1_1_out_37, space32_1_1_out_38, space32_1_1_out_39, space32_1_1_out_40, space32_1_1_out_41,
       space32_1_1_out_42, space32_1_1_out_43, space32_1_1_out_44, space32_1_1_out_45, space32_1_1_out_46,
       space32_1_1_out_47, space32_1_1_out_48, space32_1_1_out_49, space32_1_1_out_50, space32_1_1_out_51,
       space32_1_1_out_52, space32_1_1_out_53, space32_1_1_out_54, space32_1_1_out_55, space32_1_1_out_56,
       space32_1_1_out_57, space32_1_1_out_58, space32_1_1_out_59, space32_1_1_out_60, space32_1_1_out_61,
       space32_1_1_out_62, space32_1_1_out_63, space32_1_1_out_64, stADDR, stEXEC, stFETCH, stINTR;
  wire [2:0] dc3_8_1_p1;
  wire [3:0] reg4_inc_ld_1_p3, reg4_inc_ld_1_p4;

  not not_1 (not_1_out, in_1);
  or or_1 (bezadr2, INSTRUCBUS[0], INSTRUCBUS[1], INSTRUCBUS[2], INSTRUCBUS[3], INSTRUCBUS[4], INSTRUCBUS[5], INSTRUCBUS[6], INSTRUCBUS[7], INSTRUCBUS[8]);
  // REG4_INC_LD reg4_inc_ld_1: pin names not known; wires that end beside it: in_2, not_1_out, reg4_inc_ld_1_p3, reg4_inc_ld_1_p4, reg4_inc_ld_1_p5, reg4_inc_ld_1_p6
  // DC3_8 dc3_8_1: pin names not known; wires that end beside it: dc3_8_1_p1, 1'b1, bruncnd, brnotPSWSTandFETCH, brnotFCBUS, brgrinst, brbezadr2, bradr2, brjmp4
  not not_2 (reg4_inc_ld_1_p6, reg4_inc_ld_1_p5);
  ROM16x16 rom16x16_1 (
    .A6__0(reg4_inc_ld_1_p4), .CS(1'b1),
    .DOUT({reg4_inc_ld_1_p3[0], reg4_inc_ld_1_p3[1], reg4_inc_ld_1_p3[2], reg4_inc_ld_1_p3[3], dc3_8_1_p1[0], dc3_8_1_p1[1], dc3_8_1_p1[2], stEXEC, stADDR, clFETCH, ldIR15__0, ldIR31__16, rdMEM_t, ldMDR, incPC, ldMAR}));
  or or_2 (reg4_inc_ld_1_p5, bruncnd, brcnd);
  or or_3 (or_3_out, INSTRUCBUS[13], INSTRUCBUS[14], INSTRUCBUS[15], INSTRUCBUS[16], INSTRUCBUS[17], INSTRUCBUS[18], INSTRUCBUS[19]);
  or or_4 (or_4_out, ADDRBUS[2], ADDRBUS[3]);
  and and_1 (adr2, or_3_out, or_4_out);
  not not_3 (not_3_out, PSW[0]);
  not not_4 (not_4_out, PHASEFFBUS[0]);
  or or_5 (jmp4, INSTRUCBUS[9], INSTRUCBUS[10], INSTRUCBUS[11], INSTRUCBUS[12]);
  or or_6 (or_6_out, not_3_out, not_4_out);
  and and_2 (and_2_out, or_6_out, brnotPSWSTandFETCH);
  and and_3 (and_3_out, brnotFCBUS, ~in_3);  // AND_Gate
  and and_4 (and_4_out, brgrinst, INSTRUCBUS[20]);
  and and_5 (and_5_out, brbezadr2, bezadr2);
  and and_6 (and_6_out, bradr2, adr2);
  and and_7 (and_7_out, brjmp4, jmp4);
  or or_7 (brcnd, and_2_out, and_3_out, and_4_out, and_5_out, and_6_out, and_7_out);
  assign rdMEM = rdMEM_t ? 1'b1 : 1'bz;  // Controlled_Buffer controlled_buffer_1
  SIGPASS16 sigpass16_1 (
    .in_1(space32_1_1_out_64), .out_9(CMEMBUS[0]), .out_10(CMEMBUS[1]), .out_11(CMEMBUS[2]),
    .out_12(CMEMBUS[3]), .out_13(CMEMBUS[4]), .out_14(CMEMBUS[5]), .out_15(CMEMBUS[6]), .out_16(CMEMBUS[7]),
    .in_2(space32_1_1_out_63), .in_3(space32_1_1_out_62), .in_4(space32_1_1_out_61),
    .in_5(space32_1_1_out_60), .in_6(space32_1_1_out_59), .in_7(space32_1_1_out_58), .in_8(space32_1_1_out_57));
  SIGPASS16 sigpass16_2 (
    .in_1(space32_1_1_out_56), .out_9(CMEMBUS[8]), .out_10(CMEMBUS[9]), .out_11(CMEMBUS[10]),
    .out_12(CMEMBUS[11]), .out_13(CMEMBUS[12]), .out_14(CMEMBUS[13]), .out_15(CMEMBUS[14]),
    .out_16(CMEMBUS[15]), .in_2(space32_1_1_out_55), .in_3(space32_1_1_out_54), .in_4(space32_1_1_out_53),
    .in_5(space32_1_1_out_52), .in_6(space32_1_1_out_51), .in_7(space32_1_1_out_50), .in_8(space32_1_1_out_49));
  SPACE32_1 space32_1_1 (
    .in_1(decSP), .in_2(mxSP0), .in_3(mxSP1), .in_4(clDR), .in_5(mxB2), .in_6(clMDR), .in_7(mxMDR0),
    .in_8(mxMDR1), .in_9(mxMAR2), .in_10(mxPC0), .in_11(mxPC1), .in_12(ldXR1), .in_13(ldXR0), .in_14(ldBR1),
    .in_15(ldBR0), .in_16(incB), .in_17(ldAR), .in_18(ldDR), .in_19(mxADD11), .in_20(mxADD10),
    .in_21(mxADD01), .in_22(mxADD00), .in_23(mxMAR0), .in_24(mxMAR1), .in_25(mxB1), .in_26(mxB0),
    .in_27(ldB), .in_28(incPC), .in_29(ldPC), .in_30(ldMDR), .in_31(incMAR), .in_32(ldMAR),
    .out_33(space32_1_1_out_33), .out_34(space32_1_1_out_34), .out_35(space32_1_1_out_35),
    .out_36(space32_1_1_out_36), .out_37(space32_1_1_out_37), .out_38(space32_1_1_out_38),
    .out_39(space32_1_1_out_39), .out_40(space32_1_1_out_40), .out_41(space32_1_1_out_41),
    .out_42(space32_1_1_out_42), .out_43(space32_1_1_out_43), .out_44(space32_1_1_out_44),
    .out_45(space32_1_1_out_45), .out_46(space32_1_1_out_46), .out_47(space32_1_1_out_47),
    .out_48(space32_1_1_out_48), .out_49(space32_1_1_out_49), .out_50(space32_1_1_out_50),
    .out_51(space32_1_1_out_51), .out_52(space32_1_1_out_52), .out_53(space32_1_1_out_53),
    .out_54(space32_1_1_out_54), .out_55(space32_1_1_out_55), .out_56(space32_1_1_out_56),
    .out_57(space32_1_1_out_57), .out_58(space32_1_1_out_58), .out_59(space32_1_1_out_59),
    .out_60(space32_1_1_out_60), .out_61(space32_1_1_out_61), .out_62(space32_1_1_out_62),
    .out_63(space32_1_1_out_63), .out_64(space32_1_1_out_64));
  SIGPASS16 sigpass16_3 (
    .in_1(space32_1_1_out_48), .out_9(CMEMBUS[16]), .out_10(CMEMBUS[17]), .out_11(CMEMBUS[18]),
    .out_12(CMEMBUS[19]), .out_13(CMEMBUS[20]), .out_14(CMEMBUS[21]), .out_15(CMEMBUS[22]),
    .out_16(CMEMBUS[23]), .in_2(space32_1_1_out_47), .in_3(space32_1_1_out_46), .in_4(space32_1_1_out_45),
    .in_5(space32_1_1_out_44), .in_6(space32_1_1_out_43), .in_7(space32_1_1_out_42), .in_8(space32_1_1_out_41));
  SIGPASS16 sigpass16_4 (
    .in_1(space32_1_1_out_40), .out_9(CMEMBUS[24]), .out_10(CMEMBUS[25]), .out_11(CMEMBUS[26]),
    .out_12(CMEMBUS[27]), .out_13(CMEMBUS[28]), .out_14(CMEMBUS[29]), .out_15(CMEMBUS[30]),
    .out_16(CMEMBUS[31]), .in_2(space32_1_1_out_39), .in_3(space32_1_1_out_38), .in_4(space32_1_1_out_37),
    .in_5(space32_1_1_out_36), .in_6(space32_1_1_out_35), .in_7(space32_1_1_out_34), .in_8(space32_1_1_out_33));
  SIGPASS16 sigpass16_5 (
    .in_1(space8_1_1_out_16), .out_9(CREGBUS[0]), .out_10(CREGBUS[1]), .out_11(CREGBUS[2]),
    .out_12(CREGBUS[3]), .out_13(CREGBUS[4]), .out_14(CREGBUS[5]), .out_15(CREGBUS[6]), .out_16(CREGBUS[7]),
    .in_2(space8_1_1_out_15), .in_3(space8_1_1_out_14), .in_4(space8_1_1_out_13), .in_5(space8_1_1_out_12),
    .in_6(space8_1_1_out_11), .in_7(space8_1_1_out_10), .in_8(space8_1_1_out_9));
  SPACE8_1 space8_1_1 (
    .in_3(ldIR31__16), .in_4(ldIR15__0), .in_5(incDW), .in_6(ldDW), .in_7(incSP), .in_8(ldSP),
    .out_9(space8_1_1_out_9), .out_10(space8_1_1_out_10), .out_11(space8_1_1_out_11),
    .out_12(space8_1_1_out_12), .out_13(space8_1_1_out_13), .out_14(space8_1_1_out_14),
    .out_15(space8_1_1_out_15), .out_16(space8_1_1_out_16));  // open: in_1, in_2
  SIGPASS16 sigpass16_6 (
    .in_1(space8_1_2_out_16), .out_9(CFFBUS[0]), .out_10(CFFBUS[1]), .out_11(CFFBUS[2]), .out_12(CFFBUS[3]),
    .out_13(CFFBUS[4]), .out_14(CFFBUS[5]), .out_15(CFFBUS[6]), .out_16(CFFBUS[7]), .in_2(space8_1_2_out_15),
    .in_3(space8_1_2_out_14), .in_4(space8_1_2_out_13), .in_5(space8_1_2_out_12), .in_6(space8_1_2_out_11),
    .in_7(space8_1_2_out_10), .in_8(space8_1_2_out_9));
  SPACE8_1 space8_1_2 (
    .in_1(clINTR), .in_2(stINTR), .in_3(clEXEC), .in_4(stEXEC), .in_5(clADDR), .in_6(stADDR), .in_7(clFETCH),
    .in_8(stFETCH), .out_9(space8_1_2_out_9), .out_10(space8_1_2_out_10), .out_11(space8_1_2_out_11),
    .out_12(space8_1_2_out_12), .out_13(space8_1_2_out_13), .out_14(space8_1_2_out_14),
    .out_15(space8_1_2_out_15), .out_16(space8_1_2_out_16));

  // Other names for the same wires on the sheet: immed = ADDRBUS[0]; memdir = ADDRBUS[1]; regdir = ADDRBUS[2];
  //   regind = ADDRBUS[3]; brpom = ADDRBUS[4]; xrpom = ADDRBUS[5]; bxpom = ADDRBUS[6]; CLK = in_2; FCBUS = in_3;
  //   HALT = INSTRUCBUS[0]; RTS = INSTRUCBUS[1]; RTI = INSTRUCBUS[2]; STBR0 = INSTRUCBUS[3]; STXR0 = INSTRUCBUS[4];
  //   STBR1 = INSTRUCBUS[5]; STXR1 = INSTRUCBUS[6]; STRCPY = INSTRUCBUS[7]; STAR = INSTRUCBUS[8];
  //   ЈNEQ = INSTRUCBUS[9]; ЈLSSU = INSTRUCBUS[10]; JLSS = INSTRUCBUS[11]; JMP = INSTRUCBUS[12]; LD = INSTRUCBUS[13];
  //   ST = INSTRUCBUS[14]; AND = INSTRUCBUS[15]; ADD = INSTRUCBUS[16]; CMP = INSTRUCBUS[17]; JSR = INSTRUCBUS[18];
  //   CLR = INSTRUCBUS[19]; grinst = INSTRUCBUS[20]; FETCH = PHASEFFBUS[0]; PSWST = PSW[0]; rst = in_1

  // Notes on the sheet:
  //   Operaciona jedinica
  //   Kontrolna jedinica
endmodule

module ADDR (
  input  in_1,
  input  in_2,
  input  in_3,
  input  [3:0] PHASEFFBUS,
  input  [20:0] INSTRUCBUS,
  input  [6:0] ADDRBUS,
  output [31:0] CMEMBUS,
  output [7:0] CFFBUS,
  output [8:0] CREGBUS,
  output rdMEM
);

  wire and_1_out, and_2_out, and_3_out, bradr, brcnd, brnotADDR, brnotfcBUS, brpom, brSTORE, bruncnd, bxpom,
       clADDR, immed, ldB, ldMAR, ldMDR, memdir, mp2_4b_1_p3, mxADD00, mxADD01, mxB0, mxB1, mxMAR0, mxMAR1,
       not_1_out, rdMEM_t, reg4_inc_ld_1_p5, reg4_inc_ld_1_p6, regdir, regind, stEXEC, xrpom;
  wire [3:0] mp2_4b_1_p2, mp2_4b_1_p4, reg4_inc_ld_1_p4;
  wire [15:12] rom16x20_1_dout;

  SPACE_INV8_1 space_inv8_1_1 (
    .in_2(ADDRBUS[6]), .in_3(ADDRBUS[5]), .in_4(ADDRBUS[4]), .in_5(ADDRBUS[3]), .in_6(ADDRBUS[2]),
    .in_7(ADDRBUS[1]), .in_8(ADDRBUS[0]), .out_10(bxpom), .out_11(xrpom), .out_12(brpom), .out_13(regind),
    .out_14(regdir), .out_15(memdir), .out_16(immed));  // open: in_1, out_9
  not not_1 (not_1_out, in_1);
  // DC3_8 dc3_8_1: pin names not known; wires that end beside it: {rom16x20_1_dout[12], rom16x20_1_dout[13], rom16x20_1_dout[14]}, bruncnd, brnotADDR, bradr, brSTORE, brnotfcBUS
  // MP2_4b mp2_4b_1: pin names not known; wires that end beside it: bradr, mp2_4b_1_p2, mp2_4b_1_p3, mp2_4b_1_p4
  // REG4_INC_LD reg4_inc_ld_1: pin names not known; wires that end beside it: in_2, not_1_out, mp2_4b_1_p3, reg4_inc_ld_1_p4, reg4_inc_ld_1_p5, reg4_inc_ld_1_p6
  ROM16x20 rom16x20_1 (
    .A6__0(reg4_inc_ld_1_p4), .CS(1'b1),
    .DOUT({mp2_4b_1_p2[0], mp2_4b_1_p2[1], mp2_4b_1_p2[2], mp2_4b_1_p2[3], rom16x20_1_dout, mxADD01, mxADD00, mxMAR0, mxMAR1, ldMAR, mxB1, mxB0, stEXEC, clADDR, ldB, rdMEM_t, ldMDR}));
  or or_1 (reg4_inc_ld_1_p5, bruncnd, bradr, brcnd);
  not not_2 (reg4_inc_ld_1_p6, reg4_inc_ld_1_p5);
  REASIGN8x4 reasign8x4_1 (
    .in_1(immed), .in_2(4'b0110), .in_3(memdir), .in_4(4'b1000), .in_5(regdir), .in_6(4'b1001),
    .in_7(regind), .in_8(4'b1011), .in_9(brpom), .in_10(4'b1100), .in_11(xrpom), .in_12(4'b1101),
    .in_13(bxpom), .in_14(4'b1110), .out_17(mp2_4b_1_p4));  // open: in_15, in_16
  and and_1 (and_1_out, ~PHASEFFBUS[1], brnotADDR);  // AND_Gate
  and and_2 (and_2_out, brSTORE, INSTRUCBUS[14]);
  and and_3 (and_3_out, brnotfcBUS, ~in_3);  // AND_Gate
  or or_2 (brcnd, and_1_out, and_2_out, and_3_out);
  SIGPASS16 sigpass16_1 (
    .in_1(ldMAR), .out_9(CMEMBUS[0]), .out_11(CMEMBUS[2]), .out_14(CMEMBUS[5]), .out_15(CMEMBUS[6]),
    .out_16(CMEMBUS[7]), .in_3(ldMDR), .in_6(ldB), .in_7(mxB0), .in_8(mxB1));  // open: out_10, out_12, out_13, in_2, in_4, in_5
  SIGPASS16 sigpass16_2 (
    .in_1(mxMAR1), .out_9(CMEMBUS[8]), .out_10(CMEMBUS[9]), .out_11(CMEMBUS[10]), .out_12(CMEMBUS[11]),
    .in_2(mxMAR0), .in_3(mxADD00), .in_4(mxADD01));  // open: out_13, out_14, out_15, out_16, in_5, in_6, in_7, in_8
  SIGPASS16 sigpass16_3 (
    .out_12(CFFBUS[3]), .out_13(CFFBUS[4]), .in_4(clADDR), .in_5(stEXEC));  // open: in_1, out_9, out_10, out_11, out_14, out_15, out_16, in_2, in_3, in_6, in_7, in_8
  assign rdMEM = rdMEM_t ? 1'b1 : 1'bz;  // Controlled_Buffer controlled_buffer_1

  // Other names for the same wires on the sheet: CLK = in_2; FCBUS = in_3; STORE = INSTRUCBUS[14];
  //   ADDR = PHASEFFBUS[1]; rst = in_1

  // Notes on the sheet:
  //   Operaciona jedinica
  //   Upravljacka jedinica
endmodule

module EXEC (
  input  in_1,
  input  in_2,
  input  in_3,
  input  [15:0] B,
  input  [15:0] in_5,
  input  [3:0] PHASEFFBUS,
  input  [20:0] INSTRUCBUS,
  input  [6:0] ADDRBUS,
  input  [15:0] PSW,
  output [15:0] A,
  output [16:0] ALU,
  output [31:0] CMEMBUS,
  output [8:0] CREGBUS,
  output [7:0] CFFBUS,
  output [6:0] CPSW,
  output rdMEM,
  output wrMEM
);

  wire ADD, aluADD, aluAND, aluSUB, AND, and_1_out, and_2_out, and_3_out, and_4_out, and_5_out, and_6_out,
       and_7_out, and_8_out, and_9_out, brcnd, brimmed, brISZERO, brnotEXEC, brnotFCBUS, brnotorjmp,
       brnotregdir, bropr, bruncnd, clDR, clEXEC, clMDR, clPSWSTART, CLR, CMP, decSP, grinst, HALT, immed,
       incB, incDW, incMAR, incPC, incSP, ISZERO, JLSS, JLSSU, JMP, JSR, LD, ldA, ldAR, ldB, ldBR0, ldBR1,
       ldC, ldDR, ldDW, ldI, ldIR15__0, ldIR31__16, ldMAR, ldMDR, ldN, ldPC, ldS, ldSP, ldV, ldXR0, ldXR1,
       ldZ, mxA0, mxADD00, mxADD01, mxADD10, mxADD11, mxB0, mxB1, mxB2, mxMAR0, mxMAR1, mxMAR2, mxMDR0,
       mxMDR1, mxPC0, mxPC1, mxSP0, mxSP1, not_1_out, not_2_out, or_1_out, orjmp, PSWC, PSWI, PSWN, PSWSTART,
       PSWV, PSWZ, rdMEM_t, regdir, RTI, RTS, space8_1_1_out_9, space8_1_1_out_10, space8_1_1_out_11,
       space8_1_1_out_12, space8_1_1_out_13, space8_1_1_out_14, space8_1_1_out_15, space8_1_1_out_16,
       space8_1_2_out_9, space8_1_2_out_10, space8_1_2_out_11, space8_1_2_out_12, space8_1_2_out_13,
       space8_1_2_out_14, space8_1_2_out_15, space8_1_2_out_16, space8_1_3_out_9, space8_1_3_out_10,
       space8_1_3_out_11, space8_1_3_out_12, space8_1_3_out_13, space8_1_3_out_14, space8_1_3_out_15,
       space8_1_3_out_16, space32_1_1_out_33, space32_1_1_out_34, space32_1_1_out_35, space32_1_1_out_36,
       space32_1_1_out_37, space32_1_1_out_38, space32_1_1_out_39, space32_1_1_out_40, space32_1_1_out_41,
       space32_1_1_out_42, space32_1_1_out_43, space32_1_1_out_44, space32_1_1_out_45, space32_1_1_out_46,
       space32_1_1_out_47, space32_1_1_out_48, space32_1_1_out_49, space32_1_1_out_50, space32_1_1_out_51,
       space32_1_1_out_52, space32_1_1_out_53, space32_1_1_out_54, space32_1_1_out_55, space32_1_1_out_56,
       space32_1_1_out_57, space32_1_1_out_58, space32_1_1_out_59, space32_1_1_out_60, space32_1_1_out_61,
       space32_1_1_out_62, space32_1_1_out_63, space32_1_1_out_64, ST, STAR, STBR0, STBR1, stINTR, STRCPY,
       STXR0, STXR1, wrMEM_t, xor_1_out, \ЈNEQ ;
  wire [3:0] dc4_16_1_p1;
  wire [5:0] mp2_6_1_out_4, reasign32x6_1_out_65, reg6_inc_ld_1_a5__0, rom64x52_1_dout1;
  wire [15:0] mp2_16_1_out_4, mp2_16_2_out_4;
  wire [25:25] rom64x52_1_dout1_2;

  SPACE_INV32_1 space_inv32_1_1 (
    .in_12(INSTRUCBUS[20]), .in_13(INSTRUCBUS[19]), .in_14(INSTRUCBUS[18]), .in_15(INSTRUCBUS[17]),
    .in_16(INSTRUCBUS[16]), .in_17(INSTRUCBUS[15]), .in_18(INSTRUCBUS[14]), .in_19(INSTRUCBUS[13]),
    .in_20(INSTRUCBUS[12]), .in_21(INSTRUCBUS[11]), .in_22(INSTRUCBUS[10]), .in_23(INSTRUCBUS[9]),
    .in_24(INSTRUCBUS[8]), .in_25(INSTRUCBUS[7]), .in_26(INSTRUCBUS[6]), .in_27(INSTRUCBUS[5]),
    .in_28(INSTRUCBUS[4]), .in_29(INSTRUCBUS[3]), .in_30(INSTRUCBUS[2]), .in_31(INSTRUCBUS[1]),
    .in_32(INSTRUCBUS[0]), .out_44(grinst), .out_45(CLR), .out_46(JSR), .out_47(CMP), .out_48(ADD),
    .out_49(AND), .out_50(ST), .out_51(LD), .out_52(JMP), .out_53(JLSS), .out_54(JLSSU), .out_55(\ЈNEQ ),
    .out_56(STAR), .out_57(STRCPY), .out_58(STXR1), .out_59(STBR1), .out_60(STXR0), .out_61(STBR0),
    .out_62(RTI), .out_63(RTS), .out_64(HALT));  // open: in_1, in_2, in_3, in_4, in_5, in_6, in_7, in_8, in_9, in_10, in_11, out_33, out_34, out_35, out_36, out_37, out_38, out_39, out_40, out_41, out_42, out_43
  SPACE_INV8_1 space_inv8_1_1 (
    .in_2(ADDRBUS[6]), .in_3(ADDRBUS[5]), .in_4(ADDRBUS[4]), .in_5(ADDRBUS[3]), .in_6(ADDRBUS[2]),
    .in_7(ADDRBUS[1]), .in_8(ADDRBUS[0]), .out_14(regdir), .out_16(immed));  // open: in_1, out_9, out_10, out_11, out_12, out_13, out_15
  SPACE_INV16_1 space_inv16_1_1 (
    .in_1(PSW[15]), .in_2(PSW[14]), .in_3(PSW[13]), .in_4(PSW[12]), .in_5(PSW[11]), .in_6(PSW[10]),
    .in_7(PSW[9]), .in_8(PSW[8]), .in_9(PSW[7]), .in_10(PSW[6]), .in_11(PSW[5]), .in_12(PSW[4]),
    .in_13(PSW[3]), .in_14(PSW[2]), .in_15(PSW[1]), .in_16(PSW[0]), .out_17(PSWI), .out_28(PSWN),
    .out_29(PSWZ), .out_30(PSWC), .out_31(PSWV), .out_32(PSWSTART));  // open: out_18, out_19, out_20, out_21, out_22, out_23, out_24, out_25, out_26, out_27
  MP2_16 mp2_16_1 (.mx0(LD), .I0(ALU[15:0]), .I1(B), .out_4(mp2_16_1_out_4));
  MP2_16 mp2_16_2 (.mx0(mxA0), .I0(mp2_16_1_out_4), .I1(in_5), .out_4(mp2_16_2_out_4));
  REG16_LD_CL reg16_ld_cl_1 (.CLK(in_2), .CL(in_1), .LD(ldA), .in_2(mp2_16_2_out_4), .out_6(A));  // open: in_1
  // DC4_16 dc4_16_1: pin names not known; wires that end beside it: dc4_16_1_p1, 1'b1, bruncnd, brnotEXEC, bropr, brnotFCBUS, brISZERO, brnotorjmp, brimmed, brnotregdir
  not not_1 (not_1_out, in_1);
  MP2_6 mp2_6_1 (.mx0(bropr), .I0(rom64x52_1_dout1), .I1(reasign32x6_1_out_65), .out_4(mp2_6_1_out_4));
  REG6_INC_LD reg6_inc_ld_1 (
    .I5__0(mp2_6_1_out_4), .LD(or_1_out), .INC(not_2_out), .mr(not_1_out), .CLK(in_2),
    .A5__0(reg6_inc_ld_1_a5__0));
  or or_1 (or_1_out, bruncnd, bropr, brcnd);
  not not_2 (not_2_out, or_1_out);
  ROM64x52 rom64x52_1 (
    .A6__0(reg6_inc_ld_1_a5__0), .CS(1'b1),
    .DOUT1({rom64x52_1_dout1[0], rom64x52_1_dout1[1], rom64x52_1_dout1[2], rom64x52_1_dout1[3], rom64x52_1_dout1[4], rom64x52_1_dout1[5], rom64x52_1_dout1_2[25], dc4_16_1_p1[0], dc4_16_1_p1[1], dc4_16_1_p1[2], dc4_16_1_p1[3], clMDR, clDR, mxPC1, decSP, mxMDR1, aluSUB, aluADD, aluAND, mxMDR0, ldDR, mxPC0, ldAR, incB, wrMEM_t, mxMAR1, incDW, mxMAR0, ldB, mxB2, ldDW, ldXR1}),
    .DOUT2({ldXR0, ldBR1, ldBR0, mxA0, ldA, ldI, ldZ, ldN, ldC, ldV, ldS, ldPC, rdMEM_t, ldMDR, ldMAR, mxMAR2, incSP, clPSWSTART, stINTR, clEXEC}));
  ALU_ADD_SUB_AND alu_add_sub_and_1 (
    .ADD(aluADD), .SUB(aluSUB), .AND(aluAND), .in_1(A), .in_2(B), .out_6(ALU[15:0]), .out_7(ALU[16]));
  REASIGN32x6 reasign32x6_1 (
    .in_1(HALT), .in_2(6'b000011), .in_3(RTS), .in_4(6'b000100), .in_5(RTI), .in_7(STBR0), .in_9(STBR1),
    .in_11(STXR0), .in_13(STXR1), .in_15(STRCPY), .out_65(reasign32x6_1_out_65), .in_6(6'b001000),
    .in_8(6'b001111), .in_10(6'b010000), .in_12(6'b010001), .in_14(6'b010010), .in_16(6'b010011),
    .in_17(STAR), .in_18(6'b011001), .in_19(\ЈNEQ ), .in_20(6'b011011), .in_21(JLSSU), .in_22(6'b011101),
    .in_23(JLSS), .in_24(6'b011110), .in_25(LD), .in_26(6'b011111), .in_27(ST), .in_28(6'b100001),
    .in_29(AND), .in_30(6'b100111), .in_31(ADD), .in_32(6'b101001), .in_33(CMP), .in_34(6'b101011),
    .in_35(JSR), .in_36(6'b101100), .in_37(CLR), .in_38(6'b101111), .in_39(JMP), .in_40(6'b011010));  // open: in_41, in_42, in_43, in_44, in_45, in_46, in_47, in_48, in_49, in_50, in_51, in_52, in_53, in_54, in_55, in_56, in_57, in_58, in_59, in_60, in_61, in_62, in_63, in_64
  xor xor_1 (xor_1_out, PSWN, PSWV);
  and and_1 (and_1_out, ~PHASEFFBUS[2], brnotEXEC);  // AND_Gate
  and and_2 (and_2_out, brISZERO, ISZERO);
  and and_3 (and_3_out, brnotFCBUS, ~in_3);  // AND_Gate
  and and_4 (and_4_out, brimmed, immed);
  and and_5 (and_5_out, brnotregdir, ~regdir);  // AND_Gate
  and and_6 (and_6_out, brnotorjmp, ~orjmp);  // AND_Gate
  Comparator #(.width(16)) comparator_1 (.a(in_5), .b({16{1'b0}}), .eq(ISZERO));  // open: gt, lt
  and and_7 (and_7_out, \ЈNEQ , ~PSWZ);  // AND_Gate
  and and_8 (and_8_out, JLSSU, PSWC);
  and and_9 (and_9_out, JLSS, xor_1_out);
  or or_2 (orjmp, and_7_out, and_8_out, and_9_out);
  or or_3 (brcnd, and_1_out, and_2_out, and_3_out, and_4_out, and_5_out, and_6_out);
  SPACE32_1 space32_1_1 (
    .in_1(decSP), .in_2(mxSP0), .in_3(mxSP1), .in_4(clDR), .in_5(mxB2), .in_6(clMDR), .in_7(mxMDR0),
    .in_8(mxMDR1), .in_9(mxMAR2), .in_10(mxPC0), .in_11(mxPC1), .in_12(ldXR1), .in_13(ldXR0), .in_14(ldBR1),
    .in_15(ldBR0), .in_16(incB), .in_17(ldAR), .in_18(ldDR), .in_19(mxADD11), .in_20(mxADD10),
    .in_21(mxADD01), .in_22(mxADD00), .in_23(mxMAR0), .in_24(mxMAR1), .in_25(mxB1), .in_26(mxB0),
    .in_27(ldB), .in_28(incPC), .in_29(ldPC), .in_30(ldMDR), .in_31(incMAR), .in_32(ldMAR),
    .out_33(space32_1_1_out_33), .out_34(space32_1_1_out_34), .out_35(space32_1_1_out_35),
    .out_36(space32_1_1_out_36), .out_37(space32_1_1_out_37), .out_38(space32_1_1_out_38),
    .out_39(space32_1_1_out_39), .out_40(space32_1_1_out_40), .out_41(space32_1_1_out_41),
    .out_42(space32_1_1_out_42), .out_43(space32_1_1_out_43), .out_44(space32_1_1_out_44),
    .out_45(space32_1_1_out_45), .out_46(space32_1_1_out_46), .out_47(space32_1_1_out_47),
    .out_48(space32_1_1_out_48), .out_49(space32_1_1_out_49), .out_50(space32_1_1_out_50),
    .out_51(space32_1_1_out_51), .out_52(space32_1_1_out_52), .out_53(space32_1_1_out_53),
    .out_54(space32_1_1_out_54), .out_55(space32_1_1_out_55), .out_56(space32_1_1_out_56),
    .out_57(space32_1_1_out_57), .out_58(space32_1_1_out_58), .out_59(space32_1_1_out_59),
    .out_60(space32_1_1_out_60), .out_61(space32_1_1_out_61), .out_62(space32_1_1_out_62),
    .out_63(space32_1_1_out_63), .out_64(space32_1_1_out_64));
  SPACE8_1 space8_1_1 (
    .in_3(ldIR31__16), .in_4(ldIR15__0), .in_5(incDW), .in_6(ldDW), .in_7(incSP), .in_8(ldSP),
    .out_9(space8_1_1_out_9), .out_10(space8_1_1_out_10), .out_11(space8_1_1_out_11),
    .out_12(space8_1_1_out_12), .out_13(space8_1_1_out_13), .out_14(space8_1_1_out_14),
    .out_15(space8_1_1_out_15), .out_16(space8_1_1_out_16));  // open: in_1, in_2
  SPACE8_1 space8_1_2 (
    .in_2(stINTR), .in_3(clEXEC), .out_9(space8_1_2_out_9), .out_10(space8_1_2_out_10),
    .out_11(space8_1_2_out_11), .out_12(space8_1_2_out_12), .out_13(space8_1_2_out_13),
    .out_14(space8_1_2_out_14), .out_15(space8_1_2_out_15), .out_16(space8_1_2_out_16));  // open: in_1, in_4, in_5, in_6, in_7, in_8
  SPACE8_1 space8_1_3 (
    .in_2(ldS), .in_3(ldI), .in_4(ldZ), .in_5(ldN), .in_6(ldC), .in_7(ldV), .in_8(clPSWSTART),
    .out_9(space8_1_3_out_9), .out_10(space8_1_3_out_10), .out_11(space8_1_3_out_11),
    .out_12(space8_1_3_out_12), .out_13(space8_1_3_out_13), .out_14(space8_1_3_out_14),
    .out_15(space8_1_3_out_15), .out_16(space8_1_3_out_16));  // open: in_1
  assign rdMEM = rdMEM_t ? 1'b1 : 1'bz;  // Controlled_Buffer controlled_buffer_1
  assign wrMEM = wrMEM_t ? 1'b1 : 1'bz;  // Controlled_Buffer controlled_buffer_2
  SIGPASS16 sigpass16_1 (
    .in_1(space32_1_1_out_64), .out_9(CMEMBUS[0]), .out_10(CMEMBUS[1]), .out_11(CMEMBUS[2]),
    .out_12(CMEMBUS[3]), .out_13(CMEMBUS[4]), .out_14(CMEMBUS[5]), .out_15(CMEMBUS[6]), .out_16(CMEMBUS[7]),
    .in_2(space32_1_1_out_63), .in_3(space32_1_1_out_62), .in_4(space32_1_1_out_61),
    .in_5(space32_1_1_out_60), .in_6(space32_1_1_out_59), .in_7(space32_1_1_out_58), .in_8(space32_1_1_out_57));
  SIGPASS16 sigpass16_2 (
    .in_1(space32_1_1_out_56), .out_9(CMEMBUS[8]), .out_10(CMEMBUS[9]), .out_11(CMEMBUS[10]),
    .out_12(CMEMBUS[11]), .out_13(CMEMBUS[12]), .out_14(CMEMBUS[13]), .out_15(CMEMBUS[14]),
    .out_16(CMEMBUS[15]), .in_2(space32_1_1_out_55), .in_3(space32_1_1_out_54), .in_4(space32_1_1_out_53),
    .in_5(space32_1_1_out_52), .in_6(space32_1_1_out_51), .in_7(space32_1_1_out_50), .in_8(space32_1_1_out_49));
  SIGPASS16 sigpass16_3 (
    .in_1(space32_1_1_out_48), .out_9(CMEMBUS[16]), .out_10(CMEMBUS[17]), .out_11(CMEMBUS[18]),
    .out_12(CMEMBUS[19]), .out_13(CMEMBUS[20]), .out_14(CMEMBUS[21]), .out_15(CMEMBUS[22]),
    .out_16(CMEMBUS[23]), .in_2(space32_1_1_out_47), .in_3(space32_1_1_out_46), .in_4(space32_1_1_out_45),
    .in_5(space32_1_1_out_44), .in_6(space32_1_1_out_43), .in_7(space32_1_1_out_42), .in_8(space32_1_1_out_41));
  SIGPASS16 sigpass16_4 (
    .in_1(space32_1_1_out_40), .out_9(CMEMBUS[24]), .out_10(CMEMBUS[25]), .out_11(CMEMBUS[26]),
    .out_12(CMEMBUS[27]), .out_13(CMEMBUS[28]), .out_14(CMEMBUS[29]), .out_15(CMEMBUS[30]),
    .out_16(CMEMBUS[31]), .in_2(space32_1_1_out_39), .in_3(space32_1_1_out_38), .in_4(space32_1_1_out_37),
    .in_5(space32_1_1_out_36), .in_6(space32_1_1_out_35), .in_7(space32_1_1_out_34), .in_8(space32_1_1_out_33));
  SIGPASS16 sigpass16_5 (
    .in_1(space8_1_1_out_16), .out_9(CREGBUS[0]), .out_10(CREGBUS[1]), .out_11(CREGBUS[2]),
    .out_12(CREGBUS[3]), .out_13(CREGBUS[4]), .out_14(CREGBUS[5]), .out_15(CREGBUS[6]), .out_16(CREGBUS[7]),
    .in_2(space8_1_1_out_15), .in_3(space8_1_1_out_14), .in_4(space8_1_1_out_13), .in_5(space8_1_1_out_12),
    .in_6(space8_1_1_out_11), .in_7(space8_1_1_out_10), .in_8(space8_1_1_out_9));
  SIGPASS16 sigpass16_6 (
    .in_1(space8_1_2_out_16), .out_9(CFFBUS[0]), .out_10(CFFBUS[1]), .out_11(CFFBUS[2]), .out_12(CFFBUS[3]),
    .out_13(CFFBUS[4]), .out_14(CFFBUS[5]), .out_15(CFFBUS[6]), .out_16(CFFBUS[7]), .in_2(space8_1_2_out_15),
    .in_3(space8_1_2_out_14), .in_4(space8_1_2_out_13), .in_5(space8_1_2_out_12), .in_6(space8_1_2_out_11),
    .in_7(space8_1_2_out_10), .in_8(space8_1_2_out_9));
  SIGPASS16 sigpass16_7 (
    .in_1(space8_1_3_out_16), .out_9(CPSW[0]), .out_10(CPSW[1]), .out_11(CPSW[2]), .out_12(CPSW[3]),
    .out_13(CPSW[4]), .out_14(CPSW[5]), .out_15(CPSW[6]), .in_2(space8_1_3_out_15), .in_3(space8_1_3_out_14),
    .in_4(space8_1_3_out_13), .in_5(space8_1_3_out_12), .in_6(space8_1_3_out_11), .in_7(space8_1_3_out_10),
    .in_8(space8_1_3_out_9));  // open: out_16

  // Other names for the same wires on the sheet: ALU_t[15:0] = ALU[15:0]; aluC = ALU[16]; CLK = in_2; FCBUS = in_3;
  //   MDR[15:0] = in_5; EXEC = PHASEFFBUS[2]; rst = in_1

  // Notes on the sheet:
  //   Operaciona jedinica
  //   Registar A
  //   Upravljacka jedinica
  //   ALU
endmodule

module INTR (
  input  in_1,
  input  in_2,
  input  in_3,
  input  [3:0] PHASEFFBUS,
  input  [20:0] INSTRUCBUS,
  input  [15:0] PSW,
  input  [7:0] intr,
  output [15:0] ADDIVTP,
  output [2:0] UEXT1__0,
  output inta,
  output [31:0] CMEMBUS,
  output [8:0] CREGBUS,
  output [7:0] CFFBUS,
  output rdMEM,
  output wrMEM
);

  wire and_2_out, and_3_out, and_4_out, brcnd, brnotFCBUS, brnotINTR, brnotPREKID, bruncnd, clDR, clINTR,
       clMDR, decSP, incB, incDW, incMAR, incPC, incSP, ldAR, ldB, ldBR0, ldBR1, ldDR, ldDW, ldIR15__0,
       ldIR31__16, ldIVTP, ldMAR, ldMDR, ldPC, ldSP, ldXR0, ldXR1, mxADD00, mxADD01, mxADD10, mxADD11, mxB0,
       mxB1, mxB2, mxMAR0, mxMAR1, mxMAR2, mxMDR0, mxMDR1, mxPC0, mxPC1, mxSP0, mxSP1, not_1_out, or_1_out,
       PREKID, rdMEM_t, reg4_inc_ld_1_p5, reg4_inc_ld_1_p6, space8_1_1_out_9, space8_1_1_out_10,
       space8_1_1_out_11, space8_1_1_out_12, space8_1_1_out_13, space8_1_1_out_14, space8_1_1_out_15,
       space8_1_1_out_16, space8_1_2_out_9, space8_1_2_out_10, space8_1_2_out_11, space8_1_2_out_12,
       space8_1_2_out_13, space8_1_2_out_14, space8_1_2_out_15, space8_1_2_out_16, space32_1_1_out_33,
       space32_1_1_out_34, space32_1_1_out_35, space32_1_1_out_36, space32_1_1_out_37, space32_1_1_out_38,
       space32_1_1_out_39, space32_1_1_out_40, space32_1_1_out_41, space32_1_1_out_42, space32_1_1_out_43,
       space32_1_1_out_44, space32_1_1_out_45, space32_1_1_out_46, space32_1_1_out_47, space32_1_1_out_48,
       space32_1_1_out_49, space32_1_1_out_50, space32_1_1_out_51, space32_1_1_out_52, space32_1_1_out_53,
       space32_1_1_out_54, space32_1_1_out_55, space32_1_1_out_56, space32_1_1_out_57, space32_1_1_out_58,
       space32_1_1_out_59, space32_1_1_out_60, space32_1_1_out_61, space32_1_1_out_62, space32_1_1_out_63,
       space32_1_1_out_64, stFETCH, wrMEM_t;
  wire [2:0] cd8_1_p12, dc3_8_1_p1;
  wire [3:0] reg4_inc_ld_1_p3, reg4_inc_ld_1_p4;
  wire [15:0] IVTP;
  wire [19:17] rom16x24_1_dout;

  and and_1 (PREKID, or_1_out, PSW[15], ~INSTRUCBUS[0]);  // AND_Gate
  not not_1 (not_1_out, in_1);
  // REG4_INC_LD reg4_inc_ld_1: pin names not known; wires that end beside it: in_2, not_1_out, reg4_inc_ld_1_p3, reg4_inc_ld_1_p4, reg4_inc_ld_1_p5, reg4_inc_ld_1_p6
  // DC3_8 dc3_8_1: pin names not known; wires that end beside it: dc3_8_1_p1, 1'b1, bruncnd, brnotINTR, brnotPREKID, brnotFCBUS
  or or_1 (or_1_out, intr[7], intr[6], intr[5], intr[4], intr[3], intr[2], intr[1], intr[0]);
  REG16_LD_CL reg16_ld_cl_1 (.CLK(in_2), .CL(in_1), .LD(ldIVTP), .out_6(IVTP));  // open: in_1, in_2
  not not_2 (reg4_inc_ld_1_p6, reg4_inc_ld_1_p5);
  ROM16x24 rom16x24_1 (
    .A6__0(reg4_inc_ld_1_p4), .CS(1'b1),
    .DOUT({reg4_inc_ld_1_p3[0], reg4_inc_ld_1_p3[1], reg4_inc_ld_1_p3[2], reg4_inc_ld_1_p3[3], rom16x24_1_dout, dc3_8_1_p1[0], dc3_8_1_p1[1], dc3_8_1_p1[2], stFETCH, clINTR, ldPC, rdMEM_t, mxMAR1, mxMAR0, mxMDR0, wrMEM_t, inta, ldMDR, mxMDR1, decSP, ldMAR, mxMAR2}));
  Pull_Resistor pull_resistor_1 (.node(ldIVTP));
  or or_2 (reg4_inc_ld_1_p5, bruncnd, brcnd);
  // CD8 cd8_1: pin names not known; wires that end beside it: intr[7], intr[6], intr[5], intr[4], intr[3], intr[2], intr[1], intr[0], 1'b1, cd8_1_p12[2], cd8_1_p12[1], cd8_1_p12[0]
  // REG3_LD reg3_ld_1: pin names not known; wires that end beside it: in_2, cd8_1_p12, UEXT1__0, inta
  // ADD16 add16_1: pin names not known; wires that end beside it: {{13{1'b0}}, UEXT1__0}, ADDIVTP, IVTP
  and and_2 (and_2_out, brnotINTR, ~PHASEFFBUS[3]);  // AND_Gate
  and and_3 (and_3_out, brnotPREKID, ~PREKID);  // AND_Gate
  and and_4 (and_4_out, brnotFCBUS, ~in_3);  // AND_Gate
  or or_3 (brcnd, and_2_out, and_3_out, and_4_out);
  SPACE32_1 space32_1_1 (
    .in_1(decSP), .in_2(mxSP0), .in_3(mxSP1), .in_4(clDR), .in_5(mxB2), .in_6(clMDR), .in_7(mxMDR0),
    .in_8(mxMDR1), .in_9(mxMAR2), .in_10(mxPC0), .in_11(mxPC1), .in_12(ldXR1), .in_13(ldXR0), .in_14(ldBR1),
    .in_15(ldBR0), .in_16(incB), .in_17(ldAR), .in_18(ldDR), .in_19(mxADD11), .in_20(mxADD10),
    .in_21(mxADD01), .in_22(mxADD00), .in_23(mxMAR0), .in_24(mxMAR1), .in_25(mxB1), .in_26(mxB0),
    .in_27(ldB), .in_28(incPC), .in_29(ldPC), .in_30(ldMDR), .in_31(incMAR), .in_32(ldMAR),
    .out_33(space32_1_1_out_33), .out_34(space32_1_1_out_34), .out_35(space32_1_1_out_35),
    .out_36(space32_1_1_out_36), .out_37(space32_1_1_out_37), .out_38(space32_1_1_out_38),
    .out_39(space32_1_1_out_39), .out_40(space32_1_1_out_40), .out_41(space32_1_1_out_41),
    .out_42(space32_1_1_out_42), .out_43(space32_1_1_out_43), .out_44(space32_1_1_out_44),
    .out_45(space32_1_1_out_45), .out_46(space32_1_1_out_46), .out_47(space32_1_1_out_47),
    .out_48(space32_1_1_out_48), .out_49(space32_1_1_out_49), .out_50(space32_1_1_out_50),
    .out_51(space32_1_1_out_51), .out_52(space32_1_1_out_52), .out_53(space32_1_1_out_53),
    .out_54(space32_1_1_out_54), .out_55(space32_1_1_out_55), .out_56(space32_1_1_out_56),
    .out_57(space32_1_1_out_57), .out_58(space32_1_1_out_58), .out_59(space32_1_1_out_59),
    .out_60(space32_1_1_out_60), .out_61(space32_1_1_out_61), .out_62(space32_1_1_out_62),
    .out_63(space32_1_1_out_63), .out_64(space32_1_1_out_64));
  SPACE8_1 space8_1_1 (
    .in_3(ldIR31__16), .in_4(ldIR15__0), .in_5(incDW), .in_6(ldDW), .in_7(incSP), .in_8(ldSP),
    .out_9(space8_1_1_out_9), .out_10(space8_1_1_out_10), .out_11(space8_1_1_out_11),
    .out_12(space8_1_1_out_12), .out_13(space8_1_1_out_13), .out_14(space8_1_1_out_14),
    .out_15(space8_1_1_out_15), .out_16(space8_1_1_out_16));  // open: in_1, in_2
  SPACE8_1 space8_1_2 (
    .in_1(clINTR), .in_8(stFETCH), .out_9(space8_1_2_out_9), .out_10(space8_1_2_out_10),
    .out_11(space8_1_2_out_11), .out_12(space8_1_2_out_12), .out_13(space8_1_2_out_13),
    .out_14(space8_1_2_out_14), .out_15(space8_1_2_out_15), .out_16(space8_1_2_out_16));  // open: in_2, in_3, in_4, in_5, in_6, in_7
  assign rdMEM = rdMEM_t ? 1'b1 : 1'bz;  // Controlled_Buffer controlled_buffer_1
  assign wrMEM = wrMEM_t ? 1'b1 : 1'bz;  // Controlled_Buffer controlled_buffer_2
  SIGPASS16 sigpass16_1 (
    .in_1(space32_1_1_out_64), .out_9(CMEMBUS[0]), .out_10(CMEMBUS[1]), .out_11(CMEMBUS[2]),
    .out_12(CMEMBUS[3]), .out_13(CMEMBUS[4]), .out_14(CMEMBUS[5]), .out_15(CMEMBUS[6]), .out_16(CMEMBUS[7]),
    .in_2(space32_1_1_out_63), .in_3(space32_1_1_out_62), .in_4(space32_1_1_out_61),
    .in_5(space32_1_1_out_60), .in_6(space32_1_1_out_59), .in_7(space32_1_1_out_58), .in_8(space32_1_1_out_57));
  SIGPASS16 sigpass16_2 (
    .in_1(space32_1_1_out_56), .out_9(CMEMBUS[8]), .out_10(CMEMBUS[9]), .out_11(CMEMBUS[10]),
    .out_12(CMEMBUS[11]), .out_13(CMEMBUS[12]), .out_14(CMEMBUS[13]), .out_15(CMEMBUS[14]),
    .out_16(CMEMBUS[15]), .in_2(space32_1_1_out_55), .in_3(space32_1_1_out_54), .in_4(space32_1_1_out_53),
    .in_5(space32_1_1_out_52), .in_6(space32_1_1_out_51), .in_7(space32_1_1_out_50), .in_8(space32_1_1_out_49));
  SIGPASS16 sigpass16_3 (
    .in_1(space32_1_1_out_48), .out_9(CMEMBUS[16]), .out_10(CMEMBUS[17]), .out_11(CMEMBUS[18]),
    .out_12(CMEMBUS[19]), .out_13(CMEMBUS[20]), .out_14(CMEMBUS[21]), .out_15(CMEMBUS[22]),
    .out_16(CMEMBUS[23]), .in_2(space32_1_1_out_47), .in_3(space32_1_1_out_46), .in_4(space32_1_1_out_45),
    .in_5(space32_1_1_out_44), .in_6(space32_1_1_out_43), .in_7(space32_1_1_out_42), .in_8(space32_1_1_out_41));
  SIGPASS16 sigpass16_4 (
    .in_1(space32_1_1_out_40), .out_9(CMEMBUS[24]), .out_10(CMEMBUS[25]), .out_11(CMEMBUS[26]),
    .out_12(CMEMBUS[27]), .out_13(CMEMBUS[28]), .out_14(CMEMBUS[29]), .out_15(CMEMBUS[30]),
    .out_16(CMEMBUS[31]), .in_2(space32_1_1_out_39), .in_3(space32_1_1_out_38), .in_4(space32_1_1_out_37),
    .in_5(space32_1_1_out_36), .in_6(space32_1_1_out_35), .in_7(space32_1_1_out_34), .in_8(space32_1_1_out_33));
  SIGPASS16 sigpass16_5 (
    .in_1(space8_1_1_out_16), .out_9(CREGBUS[0]), .out_10(CREGBUS[1]), .out_11(CREGBUS[2]),
    .out_12(CREGBUS[3]), .out_13(CREGBUS[4]), .out_14(CREGBUS[5]), .out_15(CREGBUS[6]), .out_16(CREGBUS[7]),
    .in_2(space8_1_1_out_15), .in_3(space8_1_1_out_14), .in_4(space8_1_1_out_13), .in_5(space8_1_1_out_12),
    .in_6(space8_1_1_out_11), .in_7(space8_1_1_out_10), .in_8(space8_1_1_out_9));
  SIGPASS16 sigpass16_6 (
    .in_1(space8_1_2_out_16), .out_9(CFFBUS[0]), .out_10(CFFBUS[1]), .out_11(CFFBUS[2]), .out_12(CFFBUS[3]),
    .out_13(CFFBUS[4]), .out_14(CFFBUS[5]), .out_15(CFFBUS[6]), .out_16(CFFBUS[7]), .in_2(space8_1_2_out_15),
    .in_3(space8_1_2_out_14), .in_4(space8_1_2_out_13), .in_5(space8_1_2_out_12), .in_6(space8_1_2_out_11),
    .in_7(space8_1_2_out_10), .in_8(space8_1_2_out_9));

  // Other names for the same wires on the sheet: ldBRU = inta; BR[2:0] = UEXT1__0; ADDIVTP15__0[15:0] = ADDIVTP;
  //   CLK = in_2; FCBUS = in_3; HALT = INSTRUCBUS[0]; intr3__0[7:0] = intr; INTR_t = PHASEFFBUS[3]; PSWI = PSW[15];
  //   rst = in_1

  // Notes on the sheet:
  //   Operaciona jedinica
  //   Upravljacka jedinica
endmodule

module RAM (
  input  [15:0] in_1,
  input  in_2,
  input  [15:0] in_3,
  input  in_4,
  input  in_5,
  input  in_6,
  output [15:0] out_7,
  output out_8
);

  wire and_1_out, and_2_out, CNT0, LDCNT, not_1_out, notCNT0, or_1_out, reg4_ld_sl_sr_1_p6, rsff_2_p4,
       rsff_2_p5, rsff_3_p4, rsff_3_p5, sl;
  wire [3:0] CNT, LFSR;

  // RSFF rsff_1: pin names not known; wires that end beside it: 1'b0, in_2, in_6, sl
  or or_1 (or_1_out, in_4, in_5);
  // REG4_LD_SL_SR reg4_ld_sl_sr_1: pin names not known; wires that end beside it: 1'b0, 1'b0, in_2, 4'b1111, LFSR, reg4_ld_sl_sr_1_p6, sl, in_6
  // RisingEdge risingedge_1: pin names not known; wires that end beside it: or_1_out, in_2, LDCNT
  MEM64Kx16 mem64kx16_1 (.WR_RD(in_4), .A15__0(in_1), .DIN(in_3), .CS(1'b1), .CLK(in_2), .DOUT(out_7));
  xor xor_1 (reg4_ld_sl_sr_1_p6, LFSR[2], LFSR[3]);
  and and_1 (and_1_out, CNT0, not_1_out);
  not not_1 (not_1_out, LDCNT);
  // RSFF rsff_2: pin names not known; wires that end beside it: and_1_out, in_2, LDCNT, rsff_2_p4, rsff_2_p5
  not not_2 (rsff_2_p4, in_6);
  and and_2 (and_2_out, rsff_2_p5, CNT0);
  // REG4m_DEC_LD reg4m_dec_ld_1: pin names not known; wires that end beside it: in_2, LFSR, CNT, LDCNT, notCNT0, notCNT0
  or or_2 (notCNT0, CNT[0], CNT[1], CNT[2], CNT[3]);
  // RSFF rsff_3: pin names not known; wires that end beside it: 1'b1, in_2, and_2_out, rsff_3_p4, rsff_3_p5, rsff_3_p5
  not not_3 (rsff_3_p4, in_6);
  not not_4 (CNT0, notCNT0);

  assign out_8 = 1'b1;

  // Other names for the same wires on the sheet: ADR[15:0] = in_1; CLK = in_2; DIN[15:0] = in_3; DOUT[15:0] = out_7;
  //   RDMEM = in_5; rst = in_6; WRMEM = in_4

  // Notes on the sheet:
  //   Random broj predstavlja vreme pristupa memoriji
  //   Brojac za generisanje random broja 
  //   Jedinica za generisanje function complete (fc) signala
  //   Brojac za dekrementiranje random broja
  //   radi testiranja, stavicemo instantno vreme pristupa
endmodule
